// Logisim project CPU_Harvard_Arc.circ as structural Verilog: 4 circuits, main circuit main
module main (
);

  wire CALL, CFG, CFG_RD, CLK, clock_1_out, CTR_STP1, DFR_RST, DFR_RST1, HLT, JMP, LDI, LDS, LDS1, MOV,
       MUL_MULS, NOP, not_1_out, not_2_out, not_3_out, or_1_out, or_2_out, or_3_out, or_4_out, or_5_out,
       or_8_out, or_9_out, or_10_out, or_11_out, or_13_out, or_15_out, or_16_out, or_17_out, or_18_out,
       or_19_out, RST, STS, STS1;
  wire [2:0] inst_decoder_1_src, register_8_q;
  wire [3:0] priority_encoder_1_p1, priority_encoder_2_p1;
  wire [3:1] register_11_q;
  wire [6:0] register_18_q;
  wire [6:6] or_14_out;
  wire [7:0] alu_1_carry_f, CFG_REG, counter_1_q, FLAGS, inst_decoder_1_cfg_reg,
       inst_decoder_1_port_a_in_out, inst_decoder_1_rjmp_jmp_l_add, JMP_H, register_3_q, register_12_q_2,
       register_14_q;
  wire [13:0] CALL_RET_BRN;
  wire [15:0] A_IN, ADD_OUT, ALU_OUT, B_IN, controlled_buffer_6_out, controlled_buffer_9_out,
       controlled_buffer_10_out, controlled_buffer_12_out, controlled_buffer_13_out,
       controlled_buffer_16_out, controlled_buffer_34_out, controlled_buffer_36_out, CTR_CFG, CTR_DATA,
       DATA_OUT, DATA_RAM_dout, inst_decoder_1_add_out, inst_decoder_1_data_out, inst_decoder_1_rd,
       inst_decoder_1_rs, INTERRUPT_CFG, MUL_OUT_H, PORT_A_CFG, PORT_A_DATA, PORT_B_CFG, PORT_B_DATA, RD,
       register_12_q, register_15_q, register_16_q, register_17_q, register_19_q, register_20_q, RS,
       STACK_POINTER;
  wire [23:0] CALL_RET_ADD, controlled_buffer_1_out, controlled_buffer_2_out, controlled_buffer_4_out,
       inst_decoder_1_call_ret_br_add, register_1_q;
  wire [23:8] counter_1_q_2;
  wire [23:15] register_6_q;
  wire [29:0] inst_decoder_1_rjmp;
  wire [31:0] PRG_ROM_data, register_2_q;
  wire [31:16] register_10_q;
  wire [63:0] REG_0_1_2_3, REG_4_5_6_7, REG_8_9_10_11, REG_12_13_14_15;

  or or_1 (or_1_out, register_11_q[3], register_11_q[2]);
  not not_1 (not_1_out, register_11_q[2]);
  assign controlled_buffer_1_out = or_1_out ? {register_12_q, register_12_q_2} : 24'bz;  // Controlled_Buffer controlled_buffer_1
  Clock clock_1 (.out(clock_1_out));
  Multiplexer multiplexer_1 (.in0(clock_1_out), .in1(1'b0), .out(CLK), .sel(register_11_q[1]));
  assign controlled_buffer_2_out = not_1_out ? controlled_buffer_1_out : 24'bz;  // Controlled_Buffer controlled_buffer_2
  assign controlled_buffer_2_out = register_11_q[2] ? {register_12_q, counter_1_q} : 24'bz;  // Controlled_Buffer controlled_buffer_3
  Counter #(.max('hffffff), .width(24)) counter_1 (
    .clr(DFR_RST), .load(or_1_out), .up(1'b1), .count(not_2_out), .clk(CLK), .D(controlled_buffer_2_out),
    .Q({counter_1_q_2, counter_1_q}));  // open: carry
  not not_2 (not_2_out, CTR_STP1);
  Register #(.width(24)) register_1 (
    .D({counter_1_q_2, counter_1_q}), .en(CLK), .clk(CLK), .Q(register_1_q), .clr(or_2_out));
  or or_2 (or_2_out, DFR_RST, DFR_RST, DFR_RST1);
  ROM #(.addrWidth(24), .dataWidth(32)) PRG_ROM (.addr(register_1_q), .data(PRG_ROM_data));
  Register #(.width(32)) register_2 (.D(PRG_ROM_data), .en(CLK), .clk(CLK), .Q(register_2_q), .clr(or_3_out));
  or or_3 (or_3_out, DFR_RST, DFR_RST, DFR_RST1);
  INST_DECODER inst_decoder_1 (
    .FLAGS_IN(FLAGS), .DATA_IN(register_2_q), .PORT_A_IN_OUT(inst_decoder_1_port_a_in_out[0]),
    .PORT_B_IN_OUT(inst_decoder_1_port_a_in_out[1]), .HLT(inst_decoder_1_port_a_in_out[2]),
    .RST(inst_decoder_1_port_a_in_out[3]), .NOP(inst_decoder_1_port_a_in_out[4]),
    .PORT_IN(inst_decoder_1_port_a_in_out[5]), .PORT_OUT_DATA(inst_decoder_1_port_a_in_out[6]),
    .PORT_OUT_RD(inst_decoder_1_port_a_in_out[7]), .CFG_REG(inst_decoder_1_cfg_reg),
    .CALL_RET_BR_ADD(inst_decoder_1_call_ret_br_add), .RJMP(inst_decoder_1_rjmp[0]),
    .CLC(inst_decoder_1_rjmp[1]), .CLNC(inst_decoder_1_rjmp[2]), .CLZ(inst_decoder_1_rjmp[3]),
    .CNZ(inst_decoder_1_rjmp[4]), .BRE(inst_decoder_1_rjmp[5]), .BRNE(inst_decoder_1_rjmp[6]),
    .BRC(inst_decoder_1_rjmp[7]), .BRNC(inst_decoder_1_rjmp[8]), .RET(inst_decoder_1_rjmp[9]),
    .RTC(inst_decoder_1_rjmp[10]), .RTNC(inst_decoder_1_rjmp[11]), .RTZ(inst_decoder_1_rjmp[12]),
    .RTNZ(inst_decoder_1_rjmp[13]), .CFG(inst_decoder_1_rjmp[14]), .ADD(inst_decoder_1_rjmp[15]),
    .SUB(inst_decoder_1_rjmp[16]), .MUL(inst_decoder_1_rjmp[17]), .CMP(inst_decoder_1_rjmp[18]),
    .O_R(inst_decoder_1_rjmp[19]), .A_ND(inst_decoder_1_rjmp[20]), .X_OR(inst_decoder_1_rjmp[21]),
    .SR(inst_decoder_1_rjmp[22]), .SL(inst_decoder_1_rjmp[23]), .MOV(inst_decoder_1_rjmp[24]),
    .LDS(inst_decoder_1_rjmp[25]), .STS(inst_decoder_1_rjmp[26]), .LDI(inst_decoder_1_rjmp[27]),
    .CALL(inst_decoder_1_rjmp[28]), .JMP(inst_decoder_1_rjmp[29]), .RD(inst_decoder_1_rd),
    .RS(inst_decoder_1_rs), .SRC(inst_decoder_1_src[0]), .SLC(inst_decoder_1_src[1]),
    .MULS(inst_decoder_1_src[2]), .RJMP_JMP_L_ADD(inst_decoder_1_rjmp_jmp_l_add),
    .DATA_OUT(inst_decoder_1_data_out), .ADD_OUT(inst_decoder_1_add_out));
  Register register_3 (
    .D(inst_decoder_1_port_a_in_out), .en(CLK), .clk(CLK),
    .Q({register_3_q[7:5], NOP, RST, HLT, register_3_q[1:0]}), .clr(or_5_out));
  Register register_4 (.D(inst_decoder_1_cfg_reg), .en(CLK), .clk(CLK), .Q(CFG_REG), .clr(or_5_out));
  Register #(.width(24)) register_5 (
    .D(inst_decoder_1_call_ret_br_add), .en(CLK), .clk(CLK), .Q(CALL_RET_ADD), .clr(or_5_out));
  Register #(.width(30)) register_6 (
    .D(inst_decoder_1_rjmp), .en(CLK), .clk(CLK),
    .Q({JMP, CALL, LDI, STS, LDS, MOV, register_6_q, CFG, CALL_RET_BRN}), .clr(or_5_out));
  Register #(.width(32)) register_7 (
    .D({inst_decoder_1_rs, inst_decoder_1_rd}), .en(CLK), .clk(CLK), .Q({RS, RD}), .clr(or_5_out));
  Register #(.width(3)) register_8 (.D(inst_decoder_1_src), .en(CLK), .clk(CLK), .Q(register_8_q), .clr(or_5_out));
  Register register_9 (.D(inst_decoder_1_rjmp_jmp_l_add), .en(CLK), .clk(CLK), .Q(JMP_H), .clr(or_5_out));
  Register #(.width(32)) register_10 (
    .D({inst_decoder_1_add_out, inst_decoder_1_data_out}), .en(CLK), .clk(CLK),
    .Q({register_10_q, DATA_OUT}), .clr(or_5_out));
  Register #(.width(4)) register_11 (
    .D({CTR_STP1, CALL_RET_BRN[0], HLT, RST}), .en(CLK), .clk(CLK), .Q({register_11_q, DFR_RST}),
    .clr(or_4_out));
  or or_4 (or_4_out, DFR_RST, DFR_RST);
  Register #(.width(24)) register_12 (
    .D(controlled_buffer_4_out), .en(CLK), .clk(CLK), .Q({register_12_q, register_12_q_2}), .clr(or_4_out));
  or or_5 (or_5_out, DFR_RST, DFR_RST);
  or or_6 (CTR_STP1, JMP, or_8_out);
  assign controlled_buffer_4_out = JMP ? {JMP_H, ADD_OUT} : 24'bz;  // Controlled_Buffer controlled_buffer_4
  or or_7 (DFR_RST1, CTR_STP1, or_1_out);
  or or_8 (or_8_out, CALL, CALL_RET_BRN[1], CALL_RET_BRN[2], CALL_RET_BRN[3], CALL_RET_BRN[4], CALL_RET_BRN[5], CALL_RET_BRN[6], CALL_RET_BRN[8], CALL_RET_BRN[9], CALL_RET_BRN[10], CALL_RET_BRN[11], CALL_RET_BRN[12], CALL_RET_BRN[13], CALL_RET_BRN[7]);
  assign controlled_buffer_4_out = or_8_out ? {CALL_RET_ADD[0], CALL_RET_ADD[1], CALL_RET_ADD[2], CALL_RET_ADD[3], CALL_RET_ADD[4], CALL_RET_ADD[5], CALL_RET_ADD[6], CALL_RET_ADD[7], CALL_RET_ADD[8], CALL_RET_ADD[9], CALL_RET_ADD[10], CALL_RET_ADD[11], CALL_RET_ADD[12], CALL_RET_ADD[13], CALL_RET_ADD[14], CALL_RET_ADD[15], CALL_RET_ADD[16], CALL_RET_ADD[17], CALL_RET_ADD[18], CALL_RET_ADD[19], CALL_RET_ADD[20], CALL_RET_ADD[21], CALL_RET_ADD[22], CALL_RET_ADD[23]} : 24'bz;  // Controlled_Buffer controlled_buffer_5
  or or_9 (or_9_out, register_6_q[16], register_6_q[15]);
  Pull_Resistor pull_resistor_1 (.node(A_IN));
  or or_10 (or_10_out, register_8_q[1], register_8_q[0]);
  Pull_Resistor pull_resistor_2 (.node(B_IN));
  or or_11 (or_11_out, or_10_out, register_6_q[16], register_6_q[22], register_6_q[23], register_6_q[20], register_6_q[19], register_6_q[21], register_6_q[18], or_9_out);
  or or_12 (MUL_MULS, register_8_q[2], register_6_q[17]);
  buf or_13 (or_13_out, DFR_RST);  // OR_Gate
  ALU alu_1 (
    .FLAG_WR(or_11_out), .RST_FLAG_REG(or_13_out), .MUL_EN(1'b1), .MULS(register_8_q[2]),
    .SFT_W_CRY(or_10_out), .CLK(CLK), .ALU_EN(or_11_out), .MUL(register_6_q[17]), .R_SFT(register_6_q[22]),
    .L_SFT(register_6_q[23]), .A_ND(register_6_q[20]), .O_R(register_6_q[19]), .X_OR(register_6_q[21]),
    .CMP(register_6_q[18]), .SUM(or_9_out), .SUB(register_6_q[16]), .A_IN(A_IN), .B_IN(B_IN),
    .MUL_OUT_H(MUL_OUT_H), .CARRY_F(alu_1_carry_f[0]), .NEG_F(alu_1_carry_f[1]), .CMP_F(alu_1_carry_f[2]),
    .V_F(alu_1_carry_f[3]), .ZERO_F(alu_1_carry_f[4]), .H_F(alu_1_carry_f[5]), .T_F(alu_1_carry_f[6]),
    .INT_F(alu_1_carry_f[7]), .ALU_OUT(ALU_OUT));  // open: FLAG_IN, FLAG_EDIT, INT_EN_FLAG, T_FLAG
  Register register_13 (.D(alu_1_carry_f), .en(CLK), .clk(CLK), .Q(FLAGS), .clr(or_15_out));
  or or_14 (or_14_out[6], MUL_MULS, or_11_out);
  not not_3 (not_3_out, or_11_out);
  or or_15 (or_15_out, DFR_RST, DFR_RST);
  or or_16 (or_16_out, or_11_out, MOV);
  assign controlled_buffer_6_out = LDI ? RD : 16'bz;  // Controlled_Buffer controlled_buffer_6
  assign controlled_buffer_6_out = LDS ? RD : 16'bz;  // Controlled_Buffer controlled_buffer_7
  assign controlled_buffer_6_out = or_16_out ? RD : 16'bz;  // Controlled_Buffer controlled_buffer_8
  assign controlled_buffer_9_out = or_16_out ? RS : 16'bz;  // Controlled_Buffer controlled_buffer_9
  assign controlled_buffer_10_out = STS ? RS : 16'bz;  // Controlled_Buffer controlled_buffer_10
  Pull_Resistor pull_resistor_3 (.node(CFG_RD));
  Pull_Resistor pull_resistor_4 (.node(controlled_buffer_6_out));
  Pull_Resistor pull_resistor_5 (.node(controlled_buffer_10_out));
  assign controlled_buffer_10_out = not_3_out ? controlled_buffer_9_out : 16'bz;  // Controlled_Buffer controlled_buffer_11
  Register register_14 (.D(CFG_REG), .en(CLK), .clk(CLK), .Q(register_14_q), .clr(or_17_out));
  Register #(.width(16)) register_15 (.D(DATA_OUT), .en(CLK), .clk(CLK), .Q(register_15_q), .clr(or_17_out));
  Register #(.width(16)) register_16 (.D(MUL_OUT_H), .en(CLK), .clk(CLK), .Q(register_16_q), .clr(or_17_out));
  Register #(.width(16)) register_17 (
    .D(controlled_buffer_6_out), .en(CLK), .clk(CLK), .Q(register_17_q), .clr(or_17_out));
  Register #(.width(7)) register_18 (
    .D({or_14_out[6], MUL_MULS, STS, LDS, LDI, CFG, CFG_RD}), .en(CLK), .clk(CLK),
    .Q({register_18_q[6:5], STS1, LDS1, register_18_q[2:0]}), .clr(or_17_out));
  Register #(.width(16)) register_19 (.D(ALU_OUT), .en(CLK), .clk(CLK), .Q(register_19_q), .clr(or_17_out));
  Register #(.width(16)) register_20 (
    .D(controlled_buffer_10_out), .en(CLK), .clk(CLK), .Q(register_20_q), .clr(or_17_out));
  Register #(.width(16)) register_21 (.D(register_10_q), .en(CLK), .clk(CLK), .Q(ADD_OUT), .clr(or_17_out));
  or or_17 (or_17_out, DFR_RST, DFR_RST);
  assign controlled_buffer_12_out = register_18_q[6] ? register_19_q : 16'bz;  // Controlled_Buffer controlled_buffer_12
  assign controlled_buffer_13_out = register_18_q[1] ? register_15_q : 16'bz;  // Controlled_Buffer controlled_buffer_13
  assign controlled_buffer_12_out = register_18_q[2] ? register_15_q : 16'bz;  // Controlled_Buffer controlled_buffer_14
  assign controlled_buffer_13_out = register_18_q[0] ? controlled_buffer_12_out : 16'bz;  // Controlled_Buffer controlled_buffer_15
  Pull_Resistor pull_resistor_6 (.node(controlled_buffer_12_out));
  Register #(.width(16)) register_22 (
    .D(controlled_buffer_13_out), .en(register_14_q[0]), .clk(DFR_RST), .Q(PORT_A_CFG), .clr(CLK));
  Register #(.width(16)) register_23 (
    .D(controlled_buffer_16_out), .en(register_17_q[0]), .clk(CLK), .Q(REG_12_13_14_15[63:48]), .clr(DFR_RST));
  assign controlled_buffer_16_out = register_18_q[5] ? register_16_q : 16'bz;  // Controlled_Buffer controlled_buffer_16
  assign controlled_buffer_16_out = register_17_q[0] ? controlled_buffer_12_out : 16'bz;  // Controlled_Buffer controlled_buffer_17
  Register #(.width(16)) register_24 (
    .D(controlled_buffer_12_out), .en(register_17_q[8]), .clk(CLK), .clr(DFR_RST));  // open: Q
  assign controlled_buffer_12_out = register_20_q[0] ? REG_12_13_14_15[63:48] : 16'bz;  // Controlled_Buffer controlled_buffer_18
  assign controlled_buffer_12_out = register_20_q[8] ? REG_4_5_6_7[63:48] : 16'bz;  // Controlled_Buffer controlled_buffer_19
  Register #(.width(16)) register_25 (
    .D(controlled_buffer_13_out), .en(register_14_q[1]), .clk(DFR_RST), .Q(PORT_B_CFG), .clr(CLK));
  or or_18 (or_18_out, register_17_q[1], register_18_q[5]);
  Register #(.width(16)) register_26 (
    .D(controlled_buffer_12_out), .en(or_18_out), .clk(CLK), .Q(REG_12_13_14_15[47:32]), .clr(DFR_RST));
  Register #(.width(16)) register_27 (
    .D(controlled_buffer_12_out), .en(register_17_q[9]), .clk(CLK), .clr(DFR_RST));  // open: Q
  assign controlled_buffer_12_out = register_20_q[1] ? REG_12_13_14_15[47:32] : 16'bz;  // Controlled_Buffer controlled_buffer_20
  assign controlled_buffer_12_out = register_20_q[9] ? REG_4_5_6_7[47:32] : 16'bz;  // Controlled_Buffer controlled_buffer_21
  Register #(.width(16)) register_28 (
    .D(controlled_buffer_13_out), .en(register_14_q[2]), .clk(DFR_RST), .Q(PORT_A_DATA), .clr(CLK));
  Register #(.width(16)) register_29 (
    .D(controlled_buffer_12_out), .en(register_17_q[2]), .clk(CLK), .Q(REG_12_13_14_15[31:16]), .clr(DFR_RST));
  Register #(.width(16)) register_30 (
    .D(controlled_buffer_12_out), .en(register_17_q[10]), .clk(CLK), .clr(DFR_RST));  // open: Q
  assign controlled_buffer_12_out = register_20_q[2] ? REG_12_13_14_15[31:16] : 16'bz;  // Controlled_Buffer controlled_buffer_22
  assign controlled_buffer_12_out = register_20_q[10] ? REG_4_5_6_7[31:16] : 16'bz;  // Controlled_Buffer controlled_buffer_23
  Register #(.width(16)) register_31 (
    .D(controlled_buffer_13_out), .en(register_14_q[3]), .clk(DFR_RST), .Q(PORT_B_DATA), .clr(CLK));
  Register #(.width(16)) register_32 (
    .D(controlled_buffer_12_out), .en(register_17_q[3]), .clk(CLK), .Q(REG_12_13_14_15[15:0]), .clr(DFR_RST));
  Register #(.width(16)) register_33 (
    .D(controlled_buffer_12_out), .en(register_17_q[11]), .clk(CLK), .clr(DFR_RST));  // open: Q
  assign controlled_buffer_12_out = register_20_q[3] ? REG_12_13_14_15[15:0] : 16'bz;  // Controlled_Buffer controlled_buffer_24
  assign controlled_buffer_12_out = register_20_q[11] ? REG_4_5_6_7[15:0] : 16'bz;  // Controlled_Buffer controlled_buffer_25
  Register #(.width(16)) register_34 (
    .D(controlled_buffer_13_out), .en(register_14_q[4]), .clk(DFR_RST), .Q(INTERRUPT_CFG), .clr(CLK));
  Register #(.width(16)) register_35 (
    .D(controlled_buffer_12_out), .en(register_17_q[4]), .clk(CLK), .Q(REG_8_9_10_11[63:48]), .clr(DFR_RST));
  Register #(.width(16)) register_36 (
    .D(controlled_buffer_12_out), .en(register_17_q[12]), .clk(CLK), .Q(REG_0_1_2_3[63:48]), .clr(DFR_RST));
  assign controlled_buffer_12_out = register_20_q[4] ? REG_8_9_10_11[63:48] : 16'bz;  // Controlled_Buffer controlled_buffer_26
  assign controlled_buffer_12_out = register_20_q[12] ? REG_0_1_2_3[63:48] : 16'bz;  // Controlled_Buffer controlled_buffer_27
  Register #(.width(16)) register_37 (
    .D(controlled_buffer_13_out), .en(register_14_q[5]), .clk(DFR_RST), .Q(CTR_CFG), .clr(CLK));
  Register #(.width(16)) register_38 (
    .D(controlled_buffer_12_out), .en(register_17_q[5]), .clk(CLK), .Q(REG_8_9_10_11[47:32]), .clr(DFR_RST));
  Register #(.width(16)) register_39 (
    .D(controlled_buffer_12_out), .en(register_17_q[13]), .clk(CLK), .Q(REG_0_1_2_3[47:32]), .clr(DFR_RST));
  assign controlled_buffer_12_out = register_20_q[5] ? REG_8_9_10_11[47:32] : 16'bz;  // Controlled_Buffer controlled_buffer_28
  assign controlled_buffer_12_out = register_20_q[13] ? REG_0_1_2_3[47:32] : 16'bz;  // Controlled_Buffer controlled_buffer_29
  Register #(.width(16)) register_40 (
    .D(controlled_buffer_13_out), .en(register_14_q[6]), .clk(DFR_RST), .Q(CTR_DATA), .clr(CLK));
  Register #(.width(16)) register_41 (
    .D(controlled_buffer_12_out), .en(register_17_q[6]), .clk(CLK), .Q(REG_8_9_10_11[31:16]), .clr(DFR_RST));
  Register #(.width(16)) register_42 (
    .D(controlled_buffer_12_out), .en(register_17_q[14]), .clk(CLK), .Q(REG_0_1_2_3[31:16]), .clr(DFR_RST));
  assign controlled_buffer_12_out = register_20_q[6] ? REG_8_9_10_11[31:16] : 16'bz;  // Controlled_Buffer controlled_buffer_30
  assign controlled_buffer_12_out = register_20_q[14] ? REG_0_1_2_3[31:16] : 16'bz;  // Controlled_Buffer controlled_buffer_31
  Register #(.width(16)) register_43 (
    .D(controlled_buffer_13_out), .en(register_14_q[7]), .clk(DFR_RST), .Q(STACK_POINTER), .clr(CLK));
  Register #(.width(16)) register_44 (
    .D(controlled_buffer_12_out), .en(register_17_q[7]), .clk(CLK), .Q(REG_8_9_10_11[15:0]), .clr(DFR_RST));
  Register #(.width(16)) register_45 (
    .D(controlled_buffer_12_out), .en(register_17_q[15]), .clk(CLK), .Q(REG_0_1_2_3[15:0]), .clr(DFR_RST));
  assign controlled_buffer_12_out = register_20_q[7] ? REG_8_9_10_11[15:0] : 16'bz;  // Controlled_Buffer controlled_buffer_32
  assign controlled_buffer_12_out = register_20_q[15] ? REG_0_1_2_3[15:0] : 16'bz;  // Controlled_Buffer controlled_buffer_33
  assign controlled_buffer_34_out = STS1 ? controlled_buffer_12_out : 16'bz;  // Controlled_Buffer controlled_buffer_34
  assign controlled_buffer_12_out = LDS1 ? DATA_RAM_dout : 16'bz;  // Controlled_Buffer controlled_buffer_35
  assign controlled_buffer_36_out = or_19_out ? ADD_OUT : 16'bz;  // Controlled_Buffer controlled_buffer_36
  or or_19 (or_19_out, STS1, LDS1);
  Multiplexer #(.select(4), .width(16)) multiplexer_2 (
    .in0(REG_12_13_14_15[63:48]), .in1(REG_12_13_14_15[47:32]), .in2(REG_12_13_14_15[31:16]),
    .in3(REG_12_13_14_15[15:0]), .in4(REG_8_9_10_11[63:48]), .in5(REG_8_9_10_11[47:32]),
    .in6(REG_8_9_10_11[31:16]), .in7(REG_8_9_10_11[15:0]), .in8(REG_4_5_6_7[63:48]),
    .in9(REG_4_5_6_7[47:32]), .in10(REG_4_5_6_7[31:16]), .in11(REG_4_5_6_7[15:0]), .in12(REG_0_1_2_3[63:48]),
    .in13(REG_0_1_2_3[47:32]), .in14(REG_0_1_2_3[31:16]), .in15(REG_0_1_2_3[15:0]), .out(A_IN),
    .sel(priority_encoder_1_p1));
  Multiplexer #(.select(4), .width(16)) multiplexer_3 (
    .in0(REG_12_13_14_15[63:48]), .in1(REG_12_13_14_15[47:32]), .in2(REG_12_13_14_15[31:16]),
    .in3(REG_12_13_14_15[15:0]), .in4(REG_8_9_10_11[63:48]), .in5(REG_8_9_10_11[47:32]),
    .in6(REG_8_9_10_11[31:16]), .in7(REG_8_9_10_11[15:0]), .in8(REG_4_5_6_7[63:48]),
    .in9(REG_4_5_6_7[47:32]), .in10(REG_4_5_6_7[31:16]), .in11(REG_4_5_6_7[15:0]), .in12(REG_0_1_2_3[63:48]),
    .in13(REG_0_1_2_3[47:32]), .in14(REG_0_1_2_3[31:16]), .in15(REG_0_1_2_3[15:0]), .out(B_IN),
    .sel(priority_encoder_2_p1));
  Pull_Resistor pull_resistor_7 (.node(controlled_buffer_36_out));
  Pull_Resistor pull_resistor_8 (.node(controlled_buffer_34_out));
  // Priority_Encoder #(.select(4)) priority_encoder_1: pin names not known; wires that end beside it: priority_encoder_1_p1
  // Priority_Encoder #(.select(4)) priority_encoder_2: pin names not known; wires that end beside it: priority_encoder_2_p1
  RAM #(.addrWidth(16), .dataWidth(16)) DATA_RAM (
    .addr(controlled_buffer_36_out), .we(STS1), .oe(LDS1), .clk(CLK), .din(controlled_buffer_34_out),
    .dout(DATA_RAM_dout));

  // Other names for the same wires on the sheet: RST_MAIN = DFR_RST; RJMP = CALL_RET_BRN[0]; DFR_RST2 = DFR_RST1

  // Notes on the sheet:
  //   contents of PRG_ROM (hex, n*v repeats v):
  //   d0000001 d1000001 10100000 c0100001 b2000000 f0000001
endmodule

// A1
module ALU (
  input  FLAG_WR,
  input  [7:0] FLAG_IN,
  input  FLAG_EDIT,
  input  RST_FLAG_REG,
  input  INT_EN_FLAG,
  input  MUL_EN,
  input  MULS,
  input  SFT_W_CRY,
  input  T_FLAG,
  input  CLK,
  input  ALU_EN,
  input  MUL,
  input  R_SFT,
  input  L_SFT,
  input  A_ND,
  input  O_R,
  input  X_OR,
  input  CMP,
  input  SUM,
  input  SUB,
  input  [15:0] A_IN,
  input  [15:0] B_IN,
  output [15:0] MUL_OUT_H,
  output CARRY_F,
  output NEG_F,
  output CMP_F,
  output V_F,
  output ZERO_F,
  output H_F,
  output T_F,
  output INT_F,
  output [15:0] ALU_OUT
);

  wire adder_1_cout, adder_2_cout, adder_2_out, adder_3_cout, adder_3_out, adder_4_cout, adder_4_out,
       adder_5_cout, adder_5_out, adder_6_cout, adder_7_cout, adder_7_out, adder_8_cout, adder_8_out,
       adder_9_cout, adder_9_out, adder_10_cout, adder_10_out, adder_11_cout, adder_11_out, adder_12_cout,
       adder_12_out, adder_13_cout, adder_13_out, adder_14_cout, adder_14_out, adder_15_cout, adder_15_out,
       adder_16_cout, adder_17_cout, adder_17_out, adder_18_cout, adder_18_out, adder_19_cout, adder_19_out,
       adder_20_cout, adder_20_out, adder_21_cout, adder_21_out, adder_22_cout, adder_22_out, adder_23_cout,
       adder_23_out, adder_24_cout, adder_24_out, adder_25_cout, adder_25_out, adder_26_cout, adder_26_out,
       adder_27_cout, adder_27_out, adder_28_cout, adder_29_cout, adder_29_out, adder_30_cout, adder_30_out,
       adder_31_cout, adder_31_out, adder_32_cout, adder_32_out, adder_33_cout, adder_33_out, adder_34_cout,
       adder_34_out, adder_35_cout, adder_35_out, adder_36_cout, adder_36_out, adder_37_cout, adder_37_out,
       adder_38_cout, adder_38_out, adder_39_cout, adder_39_out, adder_40_cout, adder_40_out, adder_41_cout,
       adder_41_out, adder_42_cout, adder_42_out, adder_43_cout, adder_43_out, adder_44_cout, adder_45_cout,
       adder_45_out, adder_46_cout, adder_46_out, adder_47_cout, adder_47_out, adder_48_cout, adder_48_out,
       adder_49_cout, adder_49_out, adder_50_cout, adder_50_out, adder_51_cout, adder_51_out, adder_52_cout,
       adder_52_out, adder_53_cout, adder_53_out, adder_54_cout, adder_54_out, adder_55_cout, adder_55_out,
       adder_56_cout, adder_56_out, adder_57_cout, adder_57_out, adder_58_cout, adder_58_out, adder_59_cout,
       adder_59_out, adder_60_cout, adder_60_out, adder_61_cout, adder_61_out, adder_62_cout, adder_63_cout,
       adder_63_out, adder_64_cout, adder_64_out, adder_65_cout, adder_65_out, adder_66_cout, adder_66_out,
       adder_67_cout, adder_67_out, adder_68_cout, adder_68_out, adder_69_cout, adder_69_out, adder_70_cout,
       adder_70_out, adder_71_cout, adder_71_out, adder_72_cout, adder_72_out, adder_73_cout, adder_73_out,
       adder_74_cout, adder_74_out, adder_75_cout, adder_75_out, adder_76_cout, adder_77_cout, adder_77_out,
       adder_78_cout, adder_78_out, adder_79_cout, adder_79_out, adder_80_cout, adder_80_out, adder_81_cout,
       adder_81_out, adder_82_cout, adder_82_out, adder_83_cout, adder_83_out, adder_84_cout, adder_84_out,
       adder_85_cout, adder_85_out, adder_86_cout, adder_86_out, adder_87_cout, adder_87_out, adder_88_cout,
       adder_88_out, adder_89_cout, adder_89_out, adder_90_cout, adder_90_out, adder_91_cout, adder_91_out,
       adder_92_cout, adder_92_out, adder_93_cout, adder_94_cout, adder_94_out, adder_95_cout, adder_95_out,
       adder_96_cout, adder_96_out, adder_97_cout, adder_97_out, adder_98_cout, adder_98_out, adder_99_cout,
       adder_99_out, adder_100_cout, adder_100_out, adder_101_cout, adder_101_out, adder_102_cout,
       adder_102_out, adder_103_cout, adder_103_out, adder_104_cout, adder_104_out, adder_105_cout,
       adder_105_out, adder_106_cout, adder_106_out, adder_107_cout, adder_107_out, adder_108_cout,
       adder_108_out, adder_109_cout, adder_109_out, adder_110_cout, adder_111_cout, adder_111_out,
       adder_112_cout, adder_112_out, adder_113_cout, adder_113_out, adder_114_cout, adder_114_out,
       adder_115_cout, adder_115_out, adder_116_cout, adder_116_out, adder_117_cout, adder_117_out,
       adder_118_cout, adder_118_out, adder_119_cout, adder_119_out, adder_120_cout, adder_120_out,
       adder_121_cout, adder_121_out, adder_122_cout, adder_122_out, adder_123_cout, adder_123_out,
       adder_124_cout, adder_124_out, adder_125_cout, adder_125_out, adder_126_cout, adder_127_cout,
       adder_127_out, adder_128_cout, adder_128_out, adder_129_cout, adder_129_out, adder_130_cout,
       adder_130_out, adder_131_cout, adder_131_out, adder_132_cout, adder_132_out, adder_133_cout,
       adder_133_out, adder_134_cout, adder_134_out, adder_135_cout, adder_135_out, adder_136_cout,
       adder_136_out, adder_137_cout, adder_137_out, adder_138_cout, adder_138_out, adder_139_cout,
       adder_139_out, adder_140_cout, adder_141_cout, adder_141_out, adder_142_cout, adder_142_out,
       adder_143_cout, adder_143_out, adder_144_cout, adder_144_out, adder_145_cout, adder_145_out,
       adder_146_cout, adder_146_out, adder_147_cout, adder_147_out, adder_148_cout, adder_148_out,
       adder_149_cout, adder_149_out, adder_150_cout, adder_150_out, adder_151_cout, adder_151_out,
       adder_152_cout, adder_152_out, adder_153_cout, adder_153_out, adder_154_cout, adder_154_out,
       adder_155_cout, adder_155_out, adder_156_cout, adder_157_cout, adder_157_out, adder_158_cout,
       adder_158_out, adder_159_cout, adder_159_out, adder_160_cout, adder_160_out, adder_161_cout,
       adder_161_out, adder_162_cout, adder_162_out, adder_163_cout, adder_163_out, adder_164_cout,
       adder_164_out, adder_165_cout, adder_165_out, adder_166_cout, adder_166_out, adder_167_cout,
       adder_167_out, adder_168_cout, adder_168_out, adder_169_cout, adder_169_out, adder_170_cout,
       adder_170_out, adder_171_cout, adder_171_out, adder_172_cout, adder_172_out, adder_173_cout,
       adder_174_cout, adder_174_out, adder_175_cout, adder_175_out, adder_176_cout, adder_176_out,
       adder_177_cout, adder_177_out, adder_178_cout, adder_178_out, adder_179_cout, adder_179_out,
       adder_180_cout, adder_180_out, adder_181_cout, adder_181_out, adder_182_cout, adder_182_out,
       adder_183_cout, adder_183_out, adder_184_cout, adder_184_out, adder_185_cout, adder_185_out,
       adder_186_cout, adder_186_out, adder_187_cout, adder_187_out, adder_188_cout, adder_189_cout,
       adder_189_out, adder_190_cout, adder_190_out, adder_191_cout, adder_191_out, adder_192_cout,
       adder_192_out, adder_193_cout, adder_193_out, adder_194_cout, adder_194_out, adder_195_cout,
       adder_195_out, adder_196_cout, adder_196_out, adder_197_cout, adder_197_out, adder_198_cout,
       adder_198_out, adder_199_cout, adder_199_out, adder_200_cout, adder_200_out, adder_201_cout,
       adder_201_out, adder_202_cout, adder_202_out, adder_203_cout, adder_203_out, adder_204_cout,
       adder_205_cout, adder_205_out, adder_206_cout, adder_206_out, adder_207_cout, adder_207_out,
       adder_208_cout, adder_208_out, adder_209_cout, adder_209_out, adder_210_cout, adder_210_out,
       adder_211_cout, adder_211_out, adder_212_cout, adder_212_out, adder_213_cout, adder_213_out,
       adder_214_cout, adder_214_out, adder_215_cout, adder_215_out, adder_216_cout, adder_216_out,
       adder_217_cout, adder_217_out, adder_218_cout, adder_218_out, adder_219_cout, adder_219_out,
       adder_220_cout, adder_220_out, adder_221_cout, adder_221_out, adder_222_cout, adder_223_cout,
       adder_223_out, adder_224_cout, adder_224_out, adder_225_cout, adder_226_cout, adder_226_out,
       adder_227_cout, adder_227_out, adder_228_cout, adder_228_out, adder_229_cout, adder_230_cout,
       adder_230_out, adder_231_cout, adder_231_out, adder_232_cout, adder_233_cout, adder_233_out,
       adder_234_cout, adder_234_out, adder_235_cout, adder_236_cout, adder_236_out, adder_237_cout,
       adder_237_out, adder_238_cout, adder_239_cout, adder_239_out, adder_240_cout, adder_240_out,
       adder_241_cout, adder_242_cout, adder_242_out, adder_243_cout, adder_243_out, adder_244_cout,
       adder_244_out, adder_245_cout, adder_246_cout, adder_246_out, adder_247_cout, adder_248_cout,
       adder_249_cout, adder_249_out, adder_250_cout, adder_251_cout, adder_251_out, adder_252_cout,
       adder_253_cout, adder_254_cout, adder_255_cout, adder_256_cout, adder_257_cout, adder_258_cout,
       adder_259_cout, adder_260_cout, adder_261_cout, adder_262_cout, adder_263_cout, adder_265_cout,
       adder_266_cout, adder_267_cout, adder_268_cout, adder_269_cout, adder_270_cout, adder_272_cout,
       and_1_out, and_2_out, and_3_out, and_4_out, and_5_out, and_6_out, and_7_out, and_8_out, and_9_out,
       and_10_out, and_11_out, and_12_out, and_13_out, and_14_out, and_15_out, and_16_out, and_17_out,
       and_18_out, and_19_out, and_20_out, and_21_out, and_22_out, and_23_out, and_24_out, and_25_out,
       and_26_out, and_27_out, and_28_out, and_29_out, and_30_out, and_31_out, and_32_out, and_33_out,
       and_34_out, and_35_out, and_36_out, and_37_out, and_38_out, and_39_out, and_40_out, and_41_out,
       and_42_out, and_43_out, and_44_out, and_45_out, and_46_out, and_47_out, and_48_out, and_49_out,
       and_50_out, and_51_out, and_52_out, and_53_out, and_54_out, and_55_out, and_56_out, and_57_out,
       and_58_out, and_59_out, and_60_out, and_61_out, and_62_out, and_63_out, and_64_out, and_65_out,
       and_66_out, and_67_out, and_68_out, and_69_out, and_70_out, and_71_out, and_72_out, and_73_out,
       and_74_out, and_75_out, and_76_out, and_77_out, and_78_out, and_79_out, and_80_out, and_81_out,
       and_82_out, and_83_out, and_84_out, and_85_out, and_86_out, and_87_out, and_88_out, and_89_out,
       and_90_out, and_91_out, and_92_out, and_93_out, and_94_out, and_95_out, and_96_out, and_97_out,
       and_98_out, and_99_out, and_100_out, and_101_out, and_102_out, and_103_out, and_104_out, and_105_out,
       and_106_out, and_107_out, and_108_out, and_109_out, and_110_out, and_111_out, and_112_out,
       and_113_out, and_114_out, and_115_out, and_116_out, and_117_out, and_118_out, and_119_out,
       and_120_out, and_121_out, and_122_out, and_123_out, and_124_out, and_125_out, and_126_out,
       and_127_out, and_128_out, and_129_out, and_130_out, and_131_out, and_132_out, and_133_out,
       and_134_out, and_135_out, and_136_out, and_137_out, and_138_out, and_139_out, and_140_out,
       and_141_out, and_142_out, and_143_out, and_144_out, and_145_out, and_146_out, and_147_out,
       and_148_out, and_149_out, and_150_out, and_151_out, and_152_out, and_153_out, and_154_out,
       and_155_out, and_156_out, and_157_out, and_158_out, and_159_out, and_160_out, and_161_out,
       and_162_out, and_163_out, and_164_out, and_165_out, and_166_out, and_167_out, and_168_out,
       and_169_out, and_170_out, and_171_out, and_172_out, and_173_out, and_174_out, and_175_out,
       and_176_out, and_177_out, and_178_out, and_179_out, and_180_out, and_181_out, and_182_out,
       and_183_out, and_184_out, and_185_out, and_186_out, and_187_out, and_188_out, and_189_out,
       and_190_out, and_191_out, and_192_out, and_193_out, and_194_out, and_195_out, and_196_out,
       and_197_out, and_198_out, and_199_out, and_200_out, and_201_out, and_202_out, and_203_out,
       and_204_out, and_205_out, and_206_out, and_207_out, and_208_out, and_209_out, and_210_out,
       and_211_out, and_212_out, and_213_out, and_214_out, and_215_out, and_216_out, and_217_out,
       and_218_out, and_219_out, and_220_out, and_221_out, and_222_out, and_223_out, and_224_out,
       and_225_out, and_226_out, and_227_out, and_228_out, and_229_out, and_230_out, and_231_out,
       and_232_out, and_233_out, and_234_out, and_235_out, and_236_out, and_237_out, and_238_out,
       and_239_out, and_240_out, and_241_out, and_242_out, and_243_out, and_244_out, and_245_out,
       and_246_out, and_247_out, and_248_out, and_249_out, and_250_out, and_251_out, and_252_out,
       and_253_out, and_254_out, and_255_out, and_256_out, multiplexer_3_out, nor_1_out, not_1_out,
       xor_1_out, xor_3_out, xor_4_out, xor_5_out, xor_6_out, xor_7_out, xor_8_out, xor_9_out, xor_10_out,
       xor_11_out, xor_12_out, xor_13_out, xor_14_out, xor_15_out, xor_16_out, xor_17_out, xor_18_out;
  wire [2:0] priority_encoder_1_out;
  wire [3:3] pull_resistor_1_node;
  wire [5:0] controlled_buffer_4_out;
  wire [7:0] controlled_buffer_1_out;
  wire [15:0] adder_256_out, adder_257_out, and_257_out, controlled_buffer_2_out, controlled_buffer_3_out,
       or_1_out, subtractor_1_out, xor_2_out;

  Multiplexer multiplexer_1 (.in0(adder_1_cout), .in1(xor_1_out), .out(MUL_OUT_H[15]), .sel(MULS));
  and and_1 (and_1_out, controlled_buffer_3_out[15], controlled_buffer_2_out[15]);
  Adder #(.width(1)) adder_1 (
    .a(and_1_out), .b(adder_2_cout), .out(MUL_OUT_H[14]), .cin(adder_6_cout), .cout(adder_1_cout));
  and and_2 (and_2_out, controlled_buffer_3_out[15], controlled_buffer_2_out[14]);
  Adder #(.width(1)) adder_2 (
    .a(and_2_out), .b(adder_3_cout), .out(adder_2_out), .cin(adder_8_cout), .cout(adder_2_cout));
  and and_3 (and_3_out, controlled_buffer_3_out[15], controlled_buffer_2_out[13]);
  and and_4 (and_4_out, controlled_buffer_3_out[15], controlled_buffer_2_out[12]);
  Adder #(.width(1)) adder_3 (
    .a(and_3_out), .b(adder_4_cout), .out(adder_3_out), .cin(adder_10_cout), .cout(adder_3_cout));
  and and_5 (and_5_out, controlled_buffer_3_out[15], controlled_buffer_2_out[11]);
  Adder #(.width(1)) adder_4 (
    .a(and_4_out), .b(adder_5_cout), .out(adder_4_out), .cin(adder_13_cout), .cout(adder_4_cout));
  and and_6 (and_6_out, controlled_buffer_3_out[15], controlled_buffer_2_out[10]);
  Adder #(.width(1)) adder_5 (
    .a(and_5_out), .b(adder_7_cout), .out(adder_5_out), .cin(adder_15_cout), .cout(adder_5_cout));
  and and_7 (and_7_out, controlled_buffer_3_out[14], controlled_buffer_2_out[15]);
  Adder #(.width(1)) adder_6 (
    .a(and_7_out), .b(adder_2_out), .out(MUL_OUT_H[13]), .cin(adder_16_cout), .cout(adder_6_cout));
  Adder #(.width(1)) adder_7 (
    .a(and_6_out), .b(adder_9_cout), .out(adder_7_out), .cin(adder_17_cout), .cout(adder_7_cout));
  and and_8 (and_8_out, controlled_buffer_3_out[14], controlled_buffer_2_out[14]);
  Adder #(.width(1)) adder_8 (
    .a(and_8_out), .b(adder_3_out), .out(adder_8_out), .cin(adder_18_cout), .cout(adder_8_cout));
  and and_9 (and_9_out, controlled_buffer_3_out[15], controlled_buffer_2_out[9]);
  Adder #(.width(1)) adder_9 (
    .a(and_9_out), .b(adder_11_cout), .out(adder_9_out), .cin(adder_20_cout), .cout(adder_9_cout));
  and and_10 (and_10_out, controlled_buffer_3_out[14], controlled_buffer_2_out[13]);
  Adder #(.width(1)) adder_10 (
    .a(and_10_out), .b(adder_4_out), .out(adder_10_out), .cin(adder_21_cout), .cout(adder_10_cout));
  and and_11 (and_11_out, controlled_buffer_3_out[15], controlled_buffer_2_out[8]);
  Adder #(.width(1)) adder_11 (
    .a(and_11_out), .b(adder_12_cout), .out(adder_11_out), .cin(adder_23_cout), .cout(adder_11_cout));
  and and_12 (and_12_out, controlled_buffer_3_out[14], controlled_buffer_2_out[12]);
  and and_13 (and_13_out, controlled_buffer_3_out[15], controlled_buffer_2_out[7]);
  Adder #(.width(1)) adder_12 (
    .a(and_13_out), .b(adder_14_cout), .out(adder_12_out), .cin(adder_26_cout), .cout(adder_12_cout));
  and and_14 (and_14_out, controlled_buffer_3_out[14], controlled_buffer_2_out[11]);
  Adder #(.width(1)) adder_13 (
    .a(and_12_out), .b(adder_5_out), .out(adder_13_out), .cin(adder_24_cout), .cout(adder_13_cout));
  and and_15 (and_15_out, controlled_buffer_3_out[13], controlled_buffer_2_out[15]);
  and and_16 (and_16_out, controlled_buffer_3_out[15], controlled_buffer_2_out[6]);
  Adder #(.width(1)) adder_14 (
    .a(and_16_out), .b(adder_19_cout), .out(adder_14_out), .cin(adder_30_cout), .cout(adder_14_cout));
  and and_17 (and_17_out, controlled_buffer_3_out[14], controlled_buffer_2_out[10]);
  Adder #(.width(1)) adder_15 (
    .a(and_14_out), .b(adder_7_out), .out(adder_15_out), .cin(adder_27_cout), .cout(adder_15_cout));
  and and_18 (and_18_out, controlled_buffer_3_out[13], controlled_buffer_2_out[14]);
  Adder #(.width(1)) adder_16 (
    .a(and_15_out), .b(adder_8_out), .out(MUL_OUT_H[12]), .cin(adder_28_cout), .cout(adder_16_cout));
  and and_19 (and_19_out, controlled_buffer_3_out[15], controlled_buffer_2_out[5]);
  and and_20 (and_20_out, controlled_buffer_3_out[14], controlled_buffer_2_out[9]);
  Adder #(.width(1)) adder_17 (
    .a(and_17_out), .b(adder_9_out), .out(adder_17_out), .cin(adder_31_cout), .cout(adder_17_cout));
  and and_21 (and_21_out, controlled_buffer_3_out[13], controlled_buffer_2_out[13]);
  Adder #(.width(1)) adder_18 (
    .a(and_18_out), .b(adder_10_out), .out(adder_18_out), .cin(adder_35_cout), .cout(adder_18_cout));
  and and_22 (and_22_out, controlled_buffer_3_out[15], controlled_buffer_2_out[4]);
  Adder #(.width(1)) adder_19 (
    .a(and_19_out), .b(adder_22_cout), .out(adder_19_out), .cin(adder_33_cout), .cout(adder_19_cout));
  Adder #(.width(1)) adder_20 (
    .a(and_20_out), .b(adder_11_out), .out(adder_20_out), .cin(adder_34_cout), .cout(adder_20_cout));
  and and_23 (and_23_out, controlled_buffer_3_out[13], controlled_buffer_2_out[12]);
  Adder #(.width(1)) adder_21 (
    .a(and_21_out), .b(adder_13_out), .out(adder_21_out), .cin(adder_38_cout), .cout(adder_21_cout));
  and and_24 (and_24_out, controlled_buffer_3_out[15], controlled_buffer_2_out[3]);
  Adder #(.width(1)) adder_22 (
    .a(and_22_out), .b(adder_25_cout), .out(adder_22_out), .cin(adder_39_cout), .cout(adder_22_cout));
  and and_25 (and_25_out, controlled_buffer_3_out[14], controlled_buffer_2_out[8]);
  Adder #(.width(1)) adder_23 (
    .a(and_25_out), .b(adder_12_out), .out(adder_23_out), .cin(adder_37_cout), .cout(adder_23_cout));
  Adder #(.width(1)) adder_24 (
    .a(and_23_out), .b(adder_15_out), .out(adder_24_out), .cin(adder_40_cout), .cout(adder_24_cout));
  and and_26 (and_26_out, controlled_buffer_3_out[15], controlled_buffer_2_out[2]);
  Adder #(.width(1)) adder_25 (
    .a(and_24_out), .b(adder_29_cout), .out(adder_25_out), .cin(adder_41_cout), .cout(adder_25_cout));
  and and_27 (and_27_out, controlled_buffer_3_out[14], controlled_buffer_2_out[7]);
  Adder #(.width(1)) adder_26 (
    .a(and_27_out), .b(adder_14_out), .out(adder_26_out), .cin(adder_42_cout), .cout(adder_26_cout));
  and and_28 (and_28_out, controlled_buffer_3_out[13], controlled_buffer_2_out[11]);
  Adder #(.width(1)) adder_27 (
    .a(and_28_out), .b(adder_17_out), .out(adder_27_out), .cin(adder_43_cout), .cout(adder_27_cout));
  and and_29 (and_29_out, controlled_buffer_3_out[12], controlled_buffer_2_out[15]);
  Adder #(.width(1)) adder_28 (
    .a(and_29_out), .b(adder_18_out), .out(MUL_OUT_H[11]), .cin(adder_44_cout), .cout(adder_28_cout));
  xor xor_1 (xor_1_out, controlled_buffer_2_out[15], controlled_buffer_3_out[15]);
  Adder #(.width(1)) adder_29 (
    .a(and_26_out), .b(adder_32_cout), .out(adder_29_out), .cin(adder_45_cout), .cout(adder_29_cout));
  and and_30 (and_30_out, controlled_buffer_3_out[14], controlled_buffer_2_out[6]);
  Adder #(.width(1)) adder_30 (
    .a(and_30_out), .b(adder_19_out), .out(adder_30_out), .cin(adder_46_cout), .cout(adder_30_cout));
  and and_31 (and_31_out, controlled_buffer_3_out[13], controlled_buffer_2_out[10]);
  Adder #(.width(1)) adder_31 (
    .a(and_31_out), .b(adder_20_out), .out(adder_31_out), .cin(adder_47_cout), .cout(adder_31_cout));
  and and_32 (and_32_out, controlled_buffer_3_out[12], controlled_buffer_2_out[14]);
  and and_33 (and_33_out, controlled_buffer_3_out[15], controlled_buffer_2_out[1]);
  Adder #(.width(1)) adder_32 (
    .a(and_33_out), .b(adder_36_cout), .out(adder_32_out), .cin(adder_49_cout), .cout(adder_32_cout));
  and and_34 (and_34_out, controlled_buffer_3_out[14], controlled_buffer_2_out[5]);
  Adder #(.width(1)) adder_33 (
    .a(and_34_out), .b(adder_22_out), .out(adder_33_out), .cin(adder_50_cout), .cout(adder_33_cout));
  and and_35 (and_35_out, controlled_buffer_3_out[13], controlled_buffer_2_out[9]);
  Adder #(.width(1)) adder_34 (
    .a(and_35_out), .b(adder_23_out), .out(adder_34_out), .cin(adder_51_cout), .cout(adder_34_cout));
  and and_36 (and_36_out, controlled_buffer_3_out[12], controlled_buffer_2_out[13]);
  Adder #(.width(1)) adder_35 (
    .a(and_32_out), .b(adder_21_out), .out(adder_35_out), .cin(adder_48_cout), .cout(adder_35_cout));
  and and_37 (and_37_out, controlled_buffer_3_out[15], controlled_buffer_2_out[0]);
  Adder #(.width(1)) adder_36 (.a(and_37_out), .b(1'b0), .out(adder_36_out), .cin(adder_53_cout), .cout(adder_36_cout));
  and and_38 (and_38_out, controlled_buffer_3_out[14], controlled_buffer_2_out[4]);
  and and_39 (and_39_out, controlled_buffer_3_out[13], controlled_buffer_2_out[8]);
  Adder #(.width(1)) adder_37 (
    .a(and_39_out), .b(adder_26_out), .out(adder_37_out), .cin(adder_55_cout), .cout(adder_37_cout));
  and and_40 (and_40_out, controlled_buffer_3_out[12], controlled_buffer_2_out[12]);
  Adder #(.width(1)) adder_38 (
    .a(and_36_out), .b(adder_24_out), .out(adder_38_out), .cin(adder_52_cout), .cout(adder_38_cout));
  and and_41 (and_41_out, controlled_buffer_3_out[14], controlled_buffer_2_out[3]);
  Adder #(.width(1)) adder_39 (
    .a(and_38_out), .b(adder_25_out), .out(adder_39_out), .cin(adder_54_cout), .cout(adder_39_cout));
  and and_42 (and_42_out, controlled_buffer_3_out[13], controlled_buffer_2_out[7]);
  and and_43 (and_43_out, controlled_buffer_3_out[12], controlled_buffer_2_out[11]);
  Adder #(.width(1)) adder_40 (
    .a(and_40_out), .b(adder_27_out), .out(adder_40_out), .cin(adder_56_cout), .cout(adder_40_cout));
  and and_44 (and_44_out, controlled_buffer_3_out[11], controlled_buffer_2_out[15]);
  and and_45 (and_45_out, controlled_buffer_3_out[14], controlled_buffer_2_out[2]);
  Adder #(.width(1)) adder_41 (
    .a(and_41_out), .b(adder_29_out), .out(adder_41_out), .cin(adder_57_cout), .cout(adder_41_cout));
  and and_46 (and_46_out, controlled_buffer_3_out[13], controlled_buffer_2_out[6]);
  Adder #(.width(1)) adder_42 (
    .a(and_42_out), .b(adder_30_out), .out(adder_42_out), .cin(adder_58_cout), .cout(adder_42_cout));
  Adder #(.width(1)) adder_43 (
    .a(and_43_out), .b(adder_31_out), .out(adder_43_out), .cin(adder_59_cout), .cout(adder_43_cout));
  and and_47 (and_47_out, controlled_buffer_3_out[11], controlled_buffer_2_out[14]);
  Adder #(.width(1)) adder_44 (
    .a(and_44_out), .b(adder_35_out), .out(MUL_OUT_H[10]), .cin(adder_62_cout), .cout(adder_44_cout));
  and and_48 (and_48_out, controlled_buffer_3_out[14], controlled_buffer_2_out[1]);
  Adder #(.width(1)) adder_45 (
    .a(and_45_out), .b(adder_32_out), .out(adder_45_out), .cin(adder_60_cout), .cout(adder_45_cout));
  and and_49 (and_49_out, controlled_buffer_3_out[13], controlled_buffer_2_out[5]);
  Adder #(.width(1)) adder_46 (
    .a(and_46_out), .b(adder_33_out), .out(adder_46_out), .cin(adder_64_cout), .cout(adder_46_cout));
  and and_50 (and_50_out, controlled_buffer_3_out[12], controlled_buffer_2_out[10]);
  Adder #(.width(1)) adder_47 (
    .a(and_50_out), .b(adder_34_out), .out(adder_47_out), .cin(adder_61_cout), .cout(adder_47_cout));
  Adder #(.width(1)) adder_48 (
    .a(and_47_out), .b(adder_38_out), .out(adder_48_out), .cin(adder_65_cout), .cout(adder_48_cout));
  Adder #(.width(1)) adder_49 (
    .a(and_48_out), .b(adder_36_out), .out(adder_49_out), .cin(adder_63_cout), .cout(adder_49_cout));
  and and_51 (and_51_out, controlled_buffer_3_out[13], controlled_buffer_2_out[4]);
  Adder #(.width(1)) adder_50 (
    .a(and_49_out), .b(adder_39_out), .out(adder_50_out), .cin(adder_67_cout), .cout(adder_50_cout));
  and and_52 (and_52_out, controlled_buffer_3_out[12], controlled_buffer_2_out[9]);
  Adder #(.width(1)) adder_51 (
    .a(and_52_out), .b(adder_37_out), .out(adder_51_out), .cin(adder_68_cout), .cout(adder_51_cout));
  and and_53 (and_53_out, controlled_buffer_3_out[11], controlled_buffer_2_out[13]);
  Adder #(.width(1)) adder_52 (
    .a(and_53_out), .b(adder_40_out), .out(adder_52_out), .cin(adder_69_cout), .cout(adder_52_cout));
  and and_54 (and_54_out, controlled_buffer_3_out[14], controlled_buffer_2_out[0]);
  Adder #(.width(1)) adder_53 (.a(and_54_out), .b(1'b0), .out(adder_53_out), .cin(adder_66_cout), .cout(adder_53_cout));
  Adder #(.width(1)) adder_54 (
    .a(and_51_out), .b(adder_41_out), .out(adder_54_out), .cin(adder_70_cout), .cout(adder_54_cout));
  and and_55 (and_55_out, controlled_buffer_3_out[12], controlled_buffer_2_out[8]);
  Adder #(.width(1)) adder_55 (
    .a(and_55_out), .b(adder_42_out), .out(adder_55_out), .cin(adder_71_cout), .cout(adder_55_cout));
  and and_56 (and_56_out, controlled_buffer_3_out[11], controlled_buffer_2_out[12]);
  Adder #(.width(1)) adder_56 (
    .a(and_56_out), .b(adder_43_out), .out(adder_56_out), .cin(adder_72_cout), .cout(adder_56_cout));
  and and_57 (and_57_out, controlled_buffer_3_out[13], controlled_buffer_2_out[3]);
  Adder #(.width(1)) adder_57 (
    .a(and_57_out), .b(adder_45_out), .out(adder_57_out), .cin(adder_73_cout), .cout(adder_57_cout));
  and and_58 (and_58_out, controlled_buffer_3_out[12], controlled_buffer_2_out[7]);
  Adder #(.width(1)) adder_58 (
    .a(and_58_out), .b(adder_46_out), .out(adder_58_out), .cin(adder_74_cout), .cout(adder_58_cout));
  and and_59 (and_59_out, controlled_buffer_3_out[11], controlled_buffer_2_out[11]);
  Adder #(.width(1)) adder_59 (
    .a(and_59_out), .b(adder_47_out), .out(adder_59_out), .cin(adder_75_cout), .cout(adder_59_cout));
  and and_60 (and_60_out, controlled_buffer_3_out[10], controlled_buffer_2_out[15]);
  and and_61 (and_61_out, controlled_buffer_3_out[13], controlled_buffer_2_out[2]);
  Adder #(.width(1)) adder_60 (
    .a(and_61_out), .b(adder_49_out), .out(adder_60_out), .cin(adder_77_cout), .cout(adder_60_cout));
  and and_62 (and_62_out, controlled_buffer_3_out[12], controlled_buffer_2_out[6]);
  and and_63 (and_63_out, controlled_buffer_3_out[11], controlled_buffer_2_out[10]);
  Adder #(.width(1)) adder_61 (
    .a(and_63_out), .b(adder_51_out), .out(adder_61_out), .cin(adder_79_cout), .cout(adder_61_cout));
  and and_64 (and_64_out, controlled_buffer_3_out[10], controlled_buffer_2_out[14]);
  Adder #(.width(1)) adder_62 (
    .a(and_60_out), .b(adder_48_out), .out(MUL_OUT_H[9]), .cin(adder_76_cout), .cout(adder_62_cout));
  and and_65 (and_65_out, controlled_buffer_3_out[13], controlled_buffer_2_out[1]);
  Adder #(.width(1)) adder_63 (
    .a(and_65_out), .b(adder_53_out), .out(adder_63_out), .cin(adder_81_cout), .cout(adder_63_cout));
  and and_66 (and_66_out, controlled_buffer_3_out[12], controlled_buffer_2_out[5]);
  Adder #(.width(1)) adder_64 (
    .a(and_62_out), .b(adder_50_out), .out(adder_64_out), .cin(adder_78_cout), .cout(adder_64_cout));
  and and_67 (and_67_out, controlled_buffer_3_out[11], controlled_buffer_2_out[9]);
  and and_68 (and_68_out, controlled_buffer_3_out[10], controlled_buffer_2_out[13]);
  Adder #(.width(1)) adder_65 (
    .a(and_64_out), .b(adder_52_out), .out(adder_65_out), .cin(adder_80_cout), .cout(adder_65_cout));
  and and_69 (and_69_out, controlled_buffer_3_out[13], controlled_buffer_2_out[0]);
  Adder #(.width(1)) adder_66 (.a(and_69_out), .b(1'b0), .out(adder_66_out), .cin(adder_85_cout), .cout(adder_66_cout));
  and and_70 (and_70_out, controlled_buffer_3_out[12], controlled_buffer_2_out[4]);
  Adder #(.width(1)) adder_67 (
    .a(and_66_out), .b(adder_54_out), .out(adder_67_out), .cin(adder_82_cout), .cout(adder_67_cout));
  and and_71 (and_71_out, controlled_buffer_3_out[11], controlled_buffer_2_out[8]);
  Adder #(.width(1)) adder_68 (
    .a(and_67_out), .b(adder_55_out), .out(adder_68_out), .cin(adder_83_cout), .cout(adder_68_cout));
  Adder #(.width(1)) adder_69 (
    .a(and_68_out), .b(adder_56_out), .out(adder_69_out), .cin(adder_84_cout), .cout(adder_69_cout));
  and and_72 (and_72_out, controlled_buffer_3_out[12], controlled_buffer_2_out[3]);
  Adder #(.width(1)) adder_70 (
    .a(and_70_out), .b(adder_57_out), .out(adder_70_out), .cin(adder_86_cout), .cout(adder_70_cout));
  and and_73 (and_73_out, controlled_buffer_3_out[11], controlled_buffer_2_out[7]);
  Adder #(.width(1)) adder_71 (
    .a(and_71_out), .b(adder_58_out), .out(adder_71_out), .cin(adder_89_cout), .cout(adder_71_cout));
  and and_74 (and_74_out, controlled_buffer_3_out[10], controlled_buffer_2_out[12]);
  Adder #(.width(1)) adder_72 (
    .a(and_74_out), .b(adder_59_out), .out(adder_72_out), .cin(adder_87_cout), .cout(adder_72_cout));
  Adder #(.width(1)) adder_73 (
    .a(and_72_out), .b(adder_60_out), .out(adder_73_out), .cin(adder_88_cout), .cout(adder_73_cout));
  and and_75 (and_75_out, controlled_buffer_3_out[11], controlled_buffer_2_out[6]);
  Adder #(.width(1)) adder_74 (
    .a(and_73_out), .b(adder_64_out), .out(adder_74_out), .cin(adder_91_cout), .cout(adder_74_cout));
  and and_76 (and_76_out, controlled_buffer_3_out[10], controlled_buffer_2_out[11]);
  Adder #(.width(1)) adder_75 (
    .a(and_76_out), .b(adder_61_out), .out(adder_75_out), .cin(adder_92_cout), .cout(adder_75_cout));
  and and_77 (and_77_out, controlled_buffer_3_out[9], controlled_buffer_2_out[15]);
  Adder #(.width(1)) adder_76 (
    .a(and_77_out), .b(adder_65_out), .out(MUL_OUT_H[8]), .cin(adder_93_cout), .cout(adder_76_cout));
  and and_78 (and_78_out, controlled_buffer_3_out[12], controlled_buffer_2_out[2]);
  Adder #(.width(1)) adder_77 (
    .a(and_78_out), .b(adder_63_out), .out(adder_77_out), .cin(adder_90_cout), .cout(adder_77_cout));
  Adder #(.width(1)) adder_78 (
    .a(and_75_out), .b(adder_67_out), .out(adder_78_out), .cin(adder_94_cout), .cout(adder_78_cout));
  and and_79 (and_79_out, controlled_buffer_3_out[10], controlled_buffer_2_out[10]);
  Adder #(.width(1)) adder_79 (
    .a(and_79_out), .b(adder_68_out), .out(adder_79_out), .cin(adder_95_cout), .cout(adder_79_cout));
  and and_80 (and_80_out, controlled_buffer_3_out[9], controlled_buffer_2_out[14]);
  Adder #(.width(1)) adder_80 (
    .a(and_80_out), .b(adder_69_out), .out(adder_80_out), .cin(adder_96_cout), .cout(adder_80_cout));
  and and_81 (and_81_out, controlled_buffer_3_out[12], controlled_buffer_2_out[1]);
  Adder #(.width(1)) adder_81 (
    .a(and_81_out), .b(adder_66_out), .out(adder_81_out), .cin(adder_97_cout), .cout(adder_81_cout));
  and and_82 (and_82_out, controlled_buffer_3_out[11], controlled_buffer_2_out[5]);
  Adder #(.width(1)) adder_82 (
    .a(and_82_out), .b(adder_70_out), .out(adder_82_out), .cin(adder_98_cout), .cout(adder_82_cout));
  and and_83 (and_83_out, controlled_buffer_3_out[10], controlled_buffer_2_out[9]);
  Adder #(.width(1)) adder_83 (
    .a(and_83_out), .b(adder_71_out), .out(adder_83_out), .cin(adder_99_cout), .cout(adder_83_cout));
  and and_84 (and_84_out, controlled_buffer_3_out[9], controlled_buffer_2_out[13]);
  Adder #(.width(1)) adder_84 (
    .a(and_84_out), .b(adder_72_out), .out(adder_84_out), .cin(adder_100_cout), .cout(adder_84_cout));
  and and_85 (and_85_out, controlled_buffer_3_out[12], controlled_buffer_2_out[0]);
  Adder #(.width(1)) adder_85 (
    .a(and_85_out), .b(1'b0), .out(adder_85_out), .cin(adder_101_cout), .cout(adder_85_cout));
  and and_86 (and_86_out, controlled_buffer_3_out[11], controlled_buffer_2_out[4]);
  Adder #(.width(1)) adder_86 (
    .a(and_86_out), .b(adder_73_out), .out(adder_86_out), .cin(adder_102_cout), .cout(adder_86_cout));
  and and_87 (and_87_out, controlled_buffer_3_out[10], controlled_buffer_2_out[8]);
  and and_88 (and_88_out, controlled_buffer_3_out[9], controlled_buffer_2_out[12]);
  Adder #(.width(1)) adder_87 (
    .a(and_88_out), .b(adder_75_out), .out(adder_87_out), .cin(adder_104_cout), .cout(adder_87_cout));
  and and_89 (and_89_out, controlled_buffer_3_out[11], controlled_buffer_2_out[3]);
  Adder #(.width(1)) adder_88 (
    .a(and_89_out), .b(adder_77_out), .out(adder_88_out), .cin(adder_105_cout), .cout(adder_88_cout));
  and and_90 (and_90_out, controlled_buffer_3_out[10], controlled_buffer_2_out[7]);
  Adder #(.width(1)) adder_89 (
    .a(and_87_out), .b(adder_74_out), .out(adder_89_out), .cin(adder_103_cout), .cout(adder_89_cout));
  and and_91 (and_91_out, controlled_buffer_3_out[9], controlled_buffer_2_out[11]);
  and and_92 (and_92_out, controlled_buffer_3_out[8], controlled_buffer_2_out[15]);
  and and_93 (and_93_out, controlled_buffer_3_out[11], controlled_buffer_2_out[2]);
  Adder #(.width(1)) adder_90 (
    .a(and_93_out), .b(adder_81_out), .out(adder_90_out), .cin(adder_108_cout), .cout(adder_90_cout));
  and and_94 (and_94_out, controlled_buffer_3_out[10], controlled_buffer_2_out[6]);
  Adder #(.width(1)) adder_91 (
    .a(and_90_out), .b(adder_78_out), .out(adder_91_out), .cin(adder_106_cout), .cout(adder_91_cout));
  and and_95 (and_95_out, controlled_buffer_3_out[9], controlled_buffer_2_out[10]);
  Adder #(.width(1)) adder_92 (
    .a(and_91_out), .b(adder_79_out), .out(adder_92_out), .cin(adder_107_cout), .cout(adder_92_cout));
  Adder #(.width(1)) adder_93 (
    .a(and_92_out), .b(adder_80_out), .out(MUL_OUT_H[7]), .cin(adder_110_cout), .cout(adder_93_cout));
  and and_96 (and_96_out, controlled_buffer_3_out[11], controlled_buffer_2_out[1]);
  and and_97 (and_97_out, controlled_buffer_3_out[10], controlled_buffer_2_out[5]);
  Adder #(.width(1)) adder_94 (
    .a(and_94_out), .b(adder_82_out), .out(adder_94_out), .cin(adder_109_cout), .cout(adder_94_cout));
  and and_98 (and_98_out, controlled_buffer_3_out[9], controlled_buffer_2_out[9]);
  Adder #(.width(1)) adder_95 (
    .a(and_95_out), .b(adder_83_out), .out(adder_95_out), .cin(adder_113_cout), .cout(adder_95_cout));
  and and_99 (and_99_out, controlled_buffer_3_out[8], controlled_buffer_2_out[14]);
  Adder #(.width(1)) adder_96 (
    .a(and_99_out), .b(adder_84_out), .out(adder_96_out), .cin(adder_114_cout), .cout(adder_96_cout));
  and and_100 (and_100_out, controlled_buffer_3_out[11], controlled_buffer_2_out[0]);
  Adder #(.width(1)) adder_97 (
    .a(and_96_out), .b(adder_85_out), .out(adder_97_out), .cin(adder_111_cout), .cout(adder_97_cout));
  Adder #(.width(1)) adder_98 (
    .a(and_97_out), .b(adder_86_out), .out(adder_98_out), .cin(adder_112_cout), .cout(adder_98_cout));
  and and_101 (and_101_out, controlled_buffer_3_out[9], controlled_buffer_2_out[8]);
  Adder #(.width(1)) adder_99 (
    .a(and_98_out), .b(adder_89_out), .out(adder_99_out), .cin(adder_116_cout), .cout(adder_99_cout));
  and and_102 (and_102_out, controlled_buffer_3_out[8], controlled_buffer_2_out[13]);
  Adder #(.width(1)) adder_100 (
    .a(and_102_out), .b(adder_87_out), .out(adder_100_out), .cin(adder_117_cout), .cout(adder_100_cout));
  Adder #(.width(1)) adder_101 (
    .a(and_100_out), .b(1'b0), .out(adder_101_out), .cin(adder_118_cout), .cout(adder_101_cout));
  and and_103 (and_103_out, controlled_buffer_3_out[10], controlled_buffer_2_out[4]);
  Adder #(.width(1)) adder_102 (
    .a(and_103_out), .b(adder_88_out), .out(adder_102_out), .cin(adder_115_cout), .cout(adder_102_cout));
  Adder #(.width(1)) adder_103 (
    .a(and_101_out), .b(adder_91_out), .out(adder_103_out), .cin(adder_119_cout), .cout(adder_103_cout));
  and and_104 (and_104_out, controlled_buffer_3_out[8], controlled_buffer_2_out[12]);
  Adder #(.width(1)) adder_104 (
    .a(and_104_out), .b(adder_92_out), .out(adder_104_out), .cin(adder_120_cout), .cout(adder_104_cout));
  and and_105 (and_105_out, controlled_buffer_3_out[10], controlled_buffer_2_out[3]);
  Adder #(.width(1)) adder_105 (
    .a(and_105_out), .b(adder_90_out), .out(adder_105_out), .cin(adder_121_cout), .cout(adder_105_cout));
  and and_106 (and_106_out, controlled_buffer_3_out[9], controlled_buffer_2_out[7]);
  Adder #(.width(1)) adder_106 (
    .a(and_106_out), .b(adder_94_out), .out(adder_106_out), .cin(adder_122_cout), .cout(adder_106_cout));
  and and_107 (and_107_out, controlled_buffer_3_out[8], controlled_buffer_2_out[11]);
  Adder #(.width(1)) adder_107 (
    .a(and_107_out), .b(adder_95_out), .out(adder_107_out), .cin(adder_125_cout), .cout(adder_107_cout));
  and and_108 (and_108_out, controlled_buffer_3_out[10], controlled_buffer_2_out[2]);
  Adder #(.width(1)) adder_108 (
    .a(and_108_out), .b(adder_97_out), .out(adder_108_out), .cin(adder_123_cout), .cout(adder_108_cout));
  and and_109 (and_109_out, controlled_buffer_3_out[9], controlled_buffer_2_out[6]);
  Adder #(.width(1)) adder_109 (
    .a(and_109_out), .b(adder_98_out), .out(adder_109_out), .cin(adder_124_cout), .cout(adder_109_cout));
  and and_110 (and_110_out, controlled_buffer_3_out[8], controlled_buffer_2_out[10]);
  and and_111 (and_111_out, controlled_buffer_3_out[7], controlled_buffer_2_out[15]);
  Adder #(.width(1)) adder_110 (
    .a(and_111_out), .b(adder_96_out), .out(MUL_OUT_H[6]), .cin(adder_126_cout), .cout(adder_110_cout));
  and and_112 (and_112_out, controlled_buffer_3_out[10], controlled_buffer_2_out[1]);
  Adder #(.width(1)) adder_111 (
    .a(and_112_out), .b(adder_101_out), .out(adder_111_out), .cin(adder_127_cout), .cout(adder_111_cout));
  and and_113 (and_113_out, controlled_buffer_3_out[9], controlled_buffer_2_out[5]);
  Adder #(.width(1)) adder_112 (
    .a(and_113_out), .b(adder_102_out), .out(adder_112_out), .cin(adder_128_cout), .cout(adder_112_cout));
  and and_114 (and_114_out, controlled_buffer_3_out[8], controlled_buffer_2_out[9]);
  Adder #(.width(1)) adder_113 (
    .a(and_110_out), .b(adder_99_out), .out(adder_113_out), .cin(adder_129_cout), .cout(adder_113_cout));
  and and_115 (and_115_out, controlled_buffer_3_out[7], controlled_buffer_2_out[14]);
  Adder #(.width(1)) adder_114 (
    .a(and_115_out), .b(adder_100_out), .out(adder_114_out), .cin(adder_130_cout), .cout(adder_114_cout));
  and and_116 (and_116_out, controlled_buffer_3_out[10], controlled_buffer_2_out[0]);
  and and_117 (and_117_out, controlled_buffer_3_out[9], controlled_buffer_2_out[4]);
  Adder #(.width(1)) adder_115 (
    .a(and_117_out), .b(adder_105_out), .out(adder_115_out), .cin(adder_132_cout), .cout(adder_115_cout));
  and and_118 (and_118_out, controlled_buffer_3_out[8], controlled_buffer_2_out[8]);
  Adder #(.width(1)) adder_116 (
    .a(and_114_out), .b(adder_103_out), .out(adder_116_out), .cin(adder_133_cout), .cout(adder_116_cout));
  and and_119 (and_119_out, controlled_buffer_3_out[7], controlled_buffer_2_out[13]);
  Adder #(.width(1)) adder_117 (
    .a(and_119_out), .b(adder_104_out), .out(adder_117_out), .cin(adder_134_cout), .cout(adder_117_cout));
  Adder #(.width(1)) adder_118 (
    .a(and_116_out), .b(1'b0), .out(adder_118_out), .cin(adder_131_cout), .cout(adder_118_cout));
  and and_120 (and_120_out, controlled_buffer_3_out[9], controlled_buffer_2_out[3]);
  and and_121 (and_121_out, controlled_buffer_3_out[8], controlled_buffer_2_out[7]);
  Adder #(.width(1)) adder_119 (
    .a(and_118_out), .b(adder_106_out), .out(adder_119_out), .cin(adder_136_cout), .cout(adder_119_cout));
  and and_122 (and_122_out, controlled_buffer_3_out[7], controlled_buffer_2_out[12]);
  Adder #(.width(1)) adder_120 (
    .a(and_122_out), .b(adder_107_out), .out(adder_120_out), .cin(adder_137_cout), .cout(adder_120_cout));
  and and_123 (and_123_out, controlled_buffer_3_out[9], controlled_buffer_2_out[2]);
  Adder #(.width(1)) adder_121 (
    .a(and_120_out), .b(adder_108_out), .out(adder_121_out), .cin(adder_135_cout), .cout(adder_121_cout));
  Adder #(.width(1)) adder_122 (
    .a(and_121_out), .b(adder_109_out), .out(adder_122_out), .cin(adder_138_cout), .cout(adder_122_cout));
  and and_124 (and_124_out, controlled_buffer_3_out[7], controlled_buffer_2_out[11]);
  and and_125 (and_125_out, controlled_buffer_3_out[6], controlled_buffer_2_out[15]);
  and and_126 (and_126_out, controlled_buffer_3_out[9], controlled_buffer_2_out[1]);
  Adder #(.width(1)) adder_123 (
    .a(and_123_out), .b(adder_111_out), .out(adder_123_out), .cin(adder_141_cout), .cout(adder_123_cout));
  and and_127 (and_127_out, controlled_buffer_3_out[8], controlled_buffer_2_out[6]);
  Adder #(.width(1)) adder_124 (
    .a(and_127_out), .b(adder_112_out), .out(adder_124_out), .cin(adder_142_cout), .cout(adder_124_cout));
  and and_128 (and_128_out, controlled_buffer_3_out[7], controlled_buffer_2_out[10]);
  Adder #(.width(1)) adder_125 (
    .a(and_124_out), .b(adder_113_out), .out(adder_125_out), .cin(adder_139_cout), .cout(adder_125_cout));
  Adder #(.width(1)) adder_126 (
    .a(and_125_out), .b(adder_114_out), .out(MUL_OUT_H[5]), .cin(adder_140_cout), .cout(adder_126_cout));
  and and_129 (and_129_out, controlled_buffer_3_out[9], controlled_buffer_2_out[0]);
  Adder #(.width(1)) adder_127 (
    .a(and_126_out), .b(adder_118_out), .out(adder_127_out), .cin(adder_144_cout), .cout(adder_127_cout));
  and and_130 (and_130_out, controlled_buffer_3_out[8], controlled_buffer_2_out[5]);
  Adder #(.width(1)) adder_128 (
    .a(and_130_out), .b(adder_115_out), .out(adder_128_out), .cin(adder_145_cout), .cout(adder_128_cout));
  and and_131 (and_131_out, controlled_buffer_3_out[7], controlled_buffer_2_out[9]);
  Adder #(.width(1)) adder_129 (
    .a(and_128_out), .b(adder_116_out), .out(adder_129_out), .cin(adder_146_cout), .cout(adder_129_cout));
  and and_132 (and_132_out, controlled_buffer_3_out[6], controlled_buffer_2_out[14]);
  Adder #(.width(1)) adder_130 (
    .a(and_132_out), .b(adder_117_out), .out(adder_130_out), .cin(adder_143_cout), .cout(adder_130_cout));
  Adder #(.width(1)) adder_131 (
    .a(and_129_out), .b(1'b0), .out(adder_131_out), .cin(adder_147_cout), .cout(adder_131_cout));
  and and_133 (and_133_out, controlled_buffer_3_out[8], controlled_buffer_2_out[4]);
  Adder #(.width(1)) adder_132 (
    .a(and_133_out), .b(adder_121_out), .out(adder_132_out), .cin(adder_148_cout), .cout(adder_132_cout));
  and and_134 (and_134_out, controlled_buffer_3_out[7], controlled_buffer_2_out[8]);
  Adder #(.width(1)) adder_133 (
    .a(and_131_out), .b(adder_119_out), .out(adder_133_out), .cin(adder_149_cout), .cout(adder_133_cout));
  and and_135 (and_135_out, controlled_buffer_3_out[6], controlled_buffer_2_out[13]);
  Adder #(.width(1)) adder_134 (
    .a(and_135_out), .b(adder_120_out), .out(adder_134_out), .cin(adder_150_cout), .cout(adder_134_cout));
  and and_136 (and_136_out, controlled_buffer_3_out[8], controlled_buffer_2_out[3]);
  Adder #(.width(1)) adder_135 (
    .a(and_136_out), .b(adder_123_out), .out(adder_135_out), .cin(adder_153_cout), .cout(adder_135_cout));
  Adder #(.width(1)) adder_136 (
    .a(and_134_out), .b(adder_122_out), .out(adder_136_out), .cin(adder_151_cout), .cout(adder_136_cout));
  and and_137 (and_137_out, controlled_buffer_3_out[6], controlled_buffer_2_out[12]);
  Adder #(.width(1)) adder_137 (
    .a(and_137_out), .b(adder_125_out), .out(adder_137_out), .cin(adder_152_cout), .cout(adder_137_cout));
  and and_138 (and_138_out, controlled_buffer_3_out[8], controlled_buffer_2_out[2]);
  and and_139 (and_139_out, controlled_buffer_3_out[7], controlled_buffer_2_out[7]);
  Adder #(.width(1)) adder_138 (
    .a(and_139_out), .b(adder_124_out), .out(adder_138_out), .cin(adder_154_cout), .cout(adder_138_cout));
  and and_140 (and_140_out, controlled_buffer_3_out[6], controlled_buffer_2_out[11]);
  Adder #(.width(1)) adder_139 (
    .a(and_140_out), .b(adder_129_out), .out(adder_139_out), .cin(adder_155_cout), .cout(adder_139_cout));
  and and_141 (and_141_out, controlled_buffer_3_out[5], controlled_buffer_2_out[15]);
  Adder #(.width(1)) adder_140 (
    .a(and_141_out), .b(adder_130_out), .out(MUL_OUT_H[4]), .cin(adder_156_cout), .cout(adder_140_cout));
  and and_142 (and_142_out, controlled_buffer_3_out[8], controlled_buffer_2_out[1]);
  Adder #(.width(1)) adder_141 (
    .a(and_138_out), .b(adder_127_out), .out(adder_141_out), .cin(adder_157_cout), .cout(adder_141_cout));
  and and_143 (and_143_out, controlled_buffer_3_out[7], controlled_buffer_2_out[6]);
  Adder #(.width(1)) adder_142 (
    .a(and_143_out), .b(adder_128_out), .out(adder_142_out), .cin(adder_158_cout), .cout(adder_142_cout));
  and and_144 (and_144_out, controlled_buffer_3_out[6], controlled_buffer_2_out[10]);
  and and_145 (and_145_out, controlled_buffer_3_out[5], controlled_buffer_2_out[14]);
  Adder #(.width(1)) adder_143 (
    .a(and_145_out), .b(adder_134_out), .out(adder_143_out), .cin(adder_160_cout), .cout(adder_143_cout));
  and and_146 (and_146_out, controlled_buffer_3_out[8], controlled_buffer_2_out[0]);
  Adder #(.width(1)) adder_144 (
    .a(and_142_out), .b(adder_131_out), .out(adder_144_out), .cin(adder_161_cout), .cout(adder_144_cout));
  and and_147 (and_147_out, controlled_buffer_3_out[7], controlled_buffer_2_out[5]);
  Adder #(.width(1)) adder_145 (
    .a(and_147_out), .b(adder_132_out), .out(adder_145_out), .cin(adder_162_cout), .cout(adder_145_cout));
  and and_148 (and_148_out, controlled_buffer_3_out[6], controlled_buffer_2_out[9]);
  Adder #(.width(1)) adder_146 (
    .a(and_144_out), .b(adder_133_out), .out(adder_146_out), .cin(adder_159_cout), .cout(adder_146_cout));
  and and_149 (and_149_out, controlled_buffer_3_out[5], controlled_buffer_2_out[13]);
  Adder #(.width(1)) adder_147 (
    .a(and_146_out), .b(1'b0), .out(adder_147_out), .cin(adder_165_cout), .cout(adder_147_cout));
  and and_150 (and_150_out, controlled_buffer_3_out[7], controlled_buffer_2_out[4]);
  Adder #(.width(1)) adder_148 (
    .a(and_150_out), .b(adder_135_out), .out(adder_148_out), .cin(adder_166_cout), .cout(adder_148_cout));
  and and_151 (and_151_out, controlled_buffer_3_out[6], controlled_buffer_2_out[8]);
  Adder #(.width(1)) adder_149 (
    .a(and_148_out), .b(adder_136_out), .out(adder_149_out), .cin(adder_163_cout), .cout(adder_149_cout));
  and and_152 (and_152_out, controlled_buffer_3_out[5], controlled_buffer_2_out[12]);
  Adder #(.width(1)) adder_150 (
    .a(and_149_out), .b(adder_137_out), .out(adder_150_out), .cin(adder_164_cout), .cout(adder_150_cout));
  and and_153 (and_153_out, controlled_buffer_3_out[7], controlled_buffer_2_out[3]);
  and and_154 (and_154_out, controlled_buffer_3_out[6], controlled_buffer_2_out[7]);
  Adder #(.width(1)) adder_151 (
    .a(and_151_out), .b(adder_138_out), .out(adder_151_out), .cin(adder_167_cout), .cout(adder_151_cout));
  and and_155 (and_155_out, controlled_buffer_3_out[5], controlled_buffer_2_out[11]);
  Adder #(.width(1)) adder_152 (
    .a(and_152_out), .b(adder_139_out), .out(adder_152_out), .cin(adder_170_cout), .cout(adder_152_cout));
  and and_156 (and_156_out, controlled_buffer_3_out[7], controlled_buffer_2_out[2]);
  Adder #(.width(1)) adder_153 (
    .a(and_153_out), .b(adder_141_out), .out(adder_153_out), .cin(adder_168_cout), .cout(adder_153_cout));
  Adder #(.width(1)) adder_154 (
    .a(and_154_out), .b(adder_142_out), .out(adder_154_out), .cin(adder_169_cout), .cout(adder_154_cout));
  and and_157 (and_157_out, controlled_buffer_3_out[5], controlled_buffer_2_out[10]);
  Adder #(.width(1)) adder_155 (
    .a(and_155_out), .b(adder_146_out), .out(adder_155_out), .cin(adder_172_cout), .cout(adder_155_cout));
  and and_158 (and_158_out, controlled_buffer_3_out[4], controlled_buffer_2_out[15]);
  Adder #(.width(1)) adder_156 (
    .a(and_158_out), .b(adder_143_out), .out(MUL_OUT_H[3]), .cin(adder_173_cout), .cout(adder_156_cout));
  and and_159 (and_159_out, controlled_buffer_3_out[7], controlled_buffer_2_out[1]);
  Adder #(.width(1)) adder_157 (
    .a(and_156_out), .b(adder_144_out), .out(adder_157_out), .cin(adder_174_cout), .cout(adder_157_cout));
  and and_160 (and_160_out, controlled_buffer_3_out[6], controlled_buffer_2_out[6]);
  Adder #(.width(1)) adder_158 (
    .a(and_160_out), .b(adder_145_out), .out(adder_158_out), .cin(adder_171_cout), .cout(adder_158_cout));
  Adder #(.width(1)) adder_159 (
    .a(and_157_out), .b(adder_149_out), .out(adder_159_out), .cin(adder_175_cout), .cout(adder_159_cout));
  and and_161 (and_161_out, controlled_buffer_3_out[4], controlled_buffer_2_out[14]);
  Adder #(.width(1)) adder_160 (
    .a(and_161_out), .b(adder_150_out), .out(adder_160_out), .cin(adder_176_cout), .cout(adder_160_cout));
  and and_162 (and_162_out, controlled_buffer_3_out[7], controlled_buffer_2_out[0]);
  Adder #(.width(1)) adder_161 (
    .a(and_159_out), .b(adder_147_out), .out(adder_161_out), .cin(adder_177_cout), .cout(adder_161_cout));
  and and_163 (and_163_out, controlled_buffer_3_out[6], controlled_buffer_2_out[5]);
  Adder #(.width(1)) adder_162 (
    .a(and_163_out), .b(adder_148_out), .out(adder_162_out), .cin(adder_178_cout), .cout(adder_162_cout));
  and and_164 (and_164_out, controlled_buffer_3_out[5], controlled_buffer_2_out[9]);
  Adder #(.width(1)) adder_163 (
    .a(and_164_out), .b(adder_151_out), .out(adder_163_out), .cin(adder_179_cout), .cout(adder_163_cout));
  and and_165 (and_165_out, controlled_buffer_3_out[4], controlled_buffer_2_out[13]);
  Adder #(.width(1)) adder_164 (
    .a(and_165_out), .b(adder_152_out), .out(adder_164_out), .cin(adder_180_cout), .cout(adder_164_cout));
  Adder #(.width(1)) adder_165 (
    .a(and_162_out), .b(1'b0), .out(adder_165_out), .cin(adder_181_cout), .cout(adder_165_cout));
  and and_166 (and_166_out, controlled_buffer_3_out[6], controlled_buffer_2_out[4]);
  Adder #(.width(1)) adder_166 (
    .a(and_166_out), .b(adder_153_out), .out(adder_166_out), .cin(adder_182_cout), .cout(adder_166_cout));
  and and_167 (and_167_out, controlled_buffer_3_out[5], controlled_buffer_2_out[8]);
  Adder #(.width(1)) adder_167 (
    .a(and_167_out), .b(adder_154_out), .out(adder_167_out), .cin(adder_183_cout), .cout(adder_167_cout));
  and and_168 (and_168_out, controlled_buffer_3_out[4], controlled_buffer_2_out[12]);
  and and_169 (and_169_out, controlled_buffer_3_out[6], controlled_buffer_2_out[3]);
  Adder #(.width(1)) adder_168 (
    .a(and_169_out), .b(adder_157_out), .out(adder_168_out), .cin(adder_185_cout), .cout(adder_168_cout));
  and and_170 (and_170_out, controlled_buffer_3_out[5], controlled_buffer_2_out[7]);
  Adder #(.width(1)) adder_169 (
    .a(and_170_out), .b(adder_158_out), .out(adder_169_out), .cin(adder_186_cout), .cout(adder_169_cout));
  and and_171 (and_171_out, controlled_buffer_3_out[4], controlled_buffer_2_out[11]);
  Adder #(.width(1)) adder_170 (
    .a(and_168_out), .b(adder_155_out), .out(adder_170_out), .cin(adder_184_cout), .cout(adder_170_cout));
  and and_172 (and_172_out, controlled_buffer_3_out[3], controlled_buffer_2_out[15]);
  and and_173 (and_173_out, controlled_buffer_3_out[6], controlled_buffer_2_out[2]);
  and and_174 (and_174_out, controlled_buffer_3_out[5], controlled_buffer_2_out[6]);
  Adder #(.width(1)) adder_171 (
    .a(and_174_out), .b(adder_162_out), .out(adder_171_out), .cin(adder_190_cout), .cout(adder_171_cout));
  and and_175 (and_175_out, controlled_buffer_3_out[4], controlled_buffer_2_out[10]);
  Adder #(.width(1)) adder_172 (
    .a(and_171_out), .b(adder_159_out), .out(adder_172_out), .cin(adder_187_cout), .cout(adder_172_cout));
  and and_176 (and_176_out, controlled_buffer_3_out[3], controlled_buffer_2_out[14]);
  Adder #(.width(1)) adder_173 (
    .a(and_172_out), .b(adder_160_out), .out(MUL_OUT_H[2]), .cin(adder_188_cout), .cout(adder_173_cout));
  and and_177 (and_177_out, controlled_buffer_3_out[6], controlled_buffer_2_out[1]);
  Adder #(.width(1)) adder_174 (
    .a(and_173_out), .b(adder_161_out), .out(adder_174_out), .cin(adder_189_cout), .cout(adder_174_cout));
  and and_178 (and_178_out, controlled_buffer_3_out[5], controlled_buffer_2_out[5]);
  and and_179 (and_179_out, controlled_buffer_3_out[4], controlled_buffer_2_out[9]);
  Adder #(.width(1)) adder_175 (
    .a(and_175_out), .b(adder_163_out), .out(adder_175_out), .cin(adder_191_cout), .cout(adder_175_cout));
  and and_180 (and_180_out, controlled_buffer_3_out[3], controlled_buffer_2_out[13]);
  Adder #(.width(1)) adder_176 (
    .a(and_176_out), .b(adder_164_out), .out(adder_176_out), .cin(adder_195_cout), .cout(adder_176_cout));
  and and_181 (and_181_out, controlled_buffer_3_out[6], controlled_buffer_2_out[0]);
  Adder #(.width(1)) adder_177 (
    .a(and_177_out), .b(adder_165_out), .out(adder_177_out), .cin(adder_192_cout), .cout(adder_177_cout));
  and and_182 (and_182_out, controlled_buffer_3_out[5], controlled_buffer_2_out[4]);
  Adder #(.width(1)) adder_178 (
    .a(and_178_out), .b(adder_166_out), .out(adder_178_out), .cin(adder_193_cout), .cout(adder_178_cout));
  Adder #(.width(1)) adder_179 (
    .a(and_179_out), .b(adder_167_out), .out(adder_179_out), .cin(adder_194_cout), .cout(adder_179_cout));
  and and_183 (and_183_out, controlled_buffer_3_out[3], controlled_buffer_2_out[12]);
  Adder #(.width(1)) adder_180 (
    .a(and_180_out), .b(adder_170_out), .out(adder_180_out), .cin(adder_198_cout), .cout(adder_180_cout));
  Adder #(.width(1)) adder_181 (
    .a(and_181_out), .b(1'b0), .out(adder_181_out), .cin(adder_196_cout), .cout(adder_181_cout));
  and and_184 (and_184_out, controlled_buffer_3_out[5], controlled_buffer_2_out[3]);
  Adder #(.width(1)) adder_182 (
    .a(and_182_out), .b(adder_168_out), .out(adder_182_out), .cin(adder_199_cout), .cout(adder_182_cout));
  and and_185 (and_185_out, controlled_buffer_3_out[4], controlled_buffer_2_out[8]);
  Adder #(.width(1)) adder_183 (
    .a(and_185_out), .b(adder_169_out), .out(adder_183_out), .cin(adder_197_cout), .cout(adder_183_cout));
  Adder #(.width(1)) adder_184 (
    .a(and_183_out), .b(adder_172_out), .out(adder_184_out), .cin(adder_200_cout), .cout(adder_184_cout));
  and and_186 (and_186_out, controlled_buffer_3_out[5], controlled_buffer_2_out[2]);
  Adder #(.width(1)) adder_185 (
    .a(and_184_out), .b(adder_174_out), .out(adder_185_out), .cin(adder_201_cout), .cout(adder_185_cout));
  and and_187 (and_187_out, controlled_buffer_3_out[4], controlled_buffer_2_out[7]);
  Adder #(.width(1)) adder_186 (
    .a(and_187_out), .b(adder_171_out), .out(adder_186_out), .cin(adder_202_cout), .cout(adder_186_cout));
  and and_188 (and_188_out, controlled_buffer_3_out[3], controlled_buffer_2_out[11]);
  Adder #(.width(1)) adder_187 (
    .a(and_188_out), .b(adder_175_out), .out(adder_187_out), .cin(adder_203_cout), .cout(adder_187_cout));
  and and_189 (and_189_out, controlled_buffer_3_out[2], controlled_buffer_2_out[15]);
  Adder #(.width(1)) adder_188 (
    .a(and_189_out), .b(adder_176_out), .out(MUL_OUT_H[1]), .cin(adder_204_cout), .cout(adder_188_cout));
  Adder #(.width(1)) adder_189 (
    .a(and_186_out), .b(adder_177_out), .out(adder_189_out), .cin(adder_205_cout), .cout(adder_189_cout));
  and and_190 (and_190_out, controlled_buffer_3_out[4], controlled_buffer_2_out[6]);
  Adder #(.width(1)) adder_190 (
    .a(and_190_out), .b(adder_178_out), .out(adder_190_out), .cin(adder_206_cout), .cout(adder_190_cout));
  and and_191 (and_191_out, controlled_buffer_3_out[3], controlled_buffer_2_out[10]);
  Adder #(.width(1)) adder_191 (
    .a(and_191_out), .b(adder_179_out), .out(adder_191_out), .cin(adder_207_cout), .cout(adder_191_cout));
  and and_192 (and_192_out, controlled_buffer_3_out[2], controlled_buffer_2_out[14]);
  and and_193 (and_193_out, controlled_buffer_3_out[5], controlled_buffer_2_out[1]);
  Adder #(.width(1)) adder_192 (
    .a(and_193_out), .b(adder_181_out), .out(adder_192_out), .cin(adder_209_cout), .cout(adder_192_cout));
  and and_194 (and_194_out, controlled_buffer_3_out[4], controlled_buffer_2_out[5]);
  Adder #(.width(1)) adder_193 (
    .a(and_194_out), .b(adder_182_out), .out(adder_193_out), .cin(adder_210_cout), .cout(adder_193_cout));
  and and_195 (and_195_out, controlled_buffer_3_out[3], controlled_buffer_2_out[9]);
  Adder #(.width(1)) adder_194 (
    .a(and_195_out), .b(adder_183_out), .out(adder_194_out), .cin(adder_211_cout), .cout(adder_194_cout));
  and and_196 (and_196_out, controlled_buffer_3_out[2], controlled_buffer_2_out[13]);
  Adder #(.width(1)) adder_195 (
    .a(and_192_out), .b(adder_180_out), .out(adder_195_out), .cin(adder_208_cout), .cout(adder_195_cout));
  and and_197 (and_197_out, controlled_buffer_3_out[5], controlled_buffer_2_out[0]);
  Adder #(.width(1)) adder_196 (
    .a(and_197_out), .b(1'b0), .out(adder_196_out), .cin(adder_213_cout), .cout(adder_196_cout));
  and and_198 (and_198_out, controlled_buffer_3_out[4], controlled_buffer_2_out[4]);
  and and_199 (and_199_out, controlled_buffer_3_out[3], controlled_buffer_2_out[8]);
  Adder #(.width(1)) adder_197 (
    .a(and_199_out), .b(adder_186_out), .out(adder_197_out), .cin(adder_215_cout), .cout(adder_197_cout));
  and and_200 (and_200_out, controlled_buffer_3_out[2], controlled_buffer_2_out[12]);
  Adder #(.width(1)) adder_198 (
    .a(and_196_out), .b(adder_184_out), .out(adder_198_out), .cin(adder_212_cout), .cout(adder_198_cout));
  and and_201 (and_201_out, controlled_buffer_3_out[4], controlled_buffer_2_out[3]);
  Adder #(.width(1)) adder_199 (
    .a(and_198_out), .b(adder_185_out), .out(adder_199_out), .cin(adder_214_cout), .cout(adder_199_cout));
  and and_202 (and_202_out, controlled_buffer_3_out[3], controlled_buffer_2_out[7]);
  and and_203 (and_203_out, controlled_buffer_3_out[2], controlled_buffer_2_out[11]);
  Adder #(.width(1)) adder_200 (
    .a(and_200_out), .b(adder_187_out), .out(adder_200_out), .cin(adder_216_cout), .cout(adder_200_cout));
  and and_204 (and_204_out, controlled_buffer_3_out[1], controlled_buffer_2_out[15]);
  and and_205 (and_205_out, controlled_buffer_3_out[4], controlled_buffer_2_out[2]);
  Adder #(.width(1)) adder_201 (
    .a(and_201_out), .b(adder_189_out), .out(adder_201_out), .cin(adder_217_cout), .cout(adder_201_cout));
  and and_206 (and_206_out, controlled_buffer_3_out[3], controlled_buffer_2_out[6]);
  Adder #(.width(1)) adder_202 (
    .a(and_202_out), .b(adder_190_out), .out(adder_202_out), .cin(adder_218_cout), .cout(adder_202_cout));
  Adder #(.width(1)) adder_203 (
    .a(and_203_out), .b(adder_191_out), .out(adder_203_out), .cin(adder_219_cout), .cout(adder_203_cout));
  and and_207 (and_207_out, controlled_buffer_3_out[1], controlled_buffer_2_out[14]);
  Adder #(.width(1)) adder_204 (
    .a(and_204_out), .b(adder_195_out), .out(MUL_OUT_H[0]), .cin(adder_222_cout), .cout(adder_204_cout));
  and and_208 (and_208_out, controlled_buffer_3_out[4], controlled_buffer_2_out[1]);
  Adder #(.width(1)) adder_205 (
    .a(and_205_out), .b(adder_192_out), .out(adder_205_out), .cin(adder_220_cout), .cout(adder_205_cout));
  and and_209 (and_209_out, controlled_buffer_3_out[3], controlled_buffer_2_out[5]);
  Adder #(.width(1)) adder_206 (
    .a(and_206_out), .b(adder_193_out), .out(adder_206_out), .cin(adder_224_cout), .cout(adder_206_cout));
  and and_210 (and_210_out, controlled_buffer_3_out[2], controlled_buffer_2_out[10]);
  Adder #(.width(1)) adder_207 (
    .a(and_210_out), .b(adder_194_out), .out(adder_207_out), .cin(adder_221_cout), .cout(adder_207_cout));
  Adder #(.width(1)) adder_208 (
    .a(and_207_out), .b(adder_198_out), .out(adder_208_out), .cin(adder_225_cout), .cout(adder_208_cout));
  Adder #(.width(1)) adder_209 (
    .a(and_208_out), .b(adder_196_out), .out(adder_209_out), .cin(adder_223_cout), .cout(adder_209_cout));
  and and_211 (and_211_out, controlled_buffer_3_out[3], controlled_buffer_2_out[4]);
  Adder #(.width(1)) adder_210 (
    .a(and_209_out), .b(adder_199_out), .out(adder_210_out), .cin(adder_227_cout), .cout(adder_210_cout));
  and and_212 (and_212_out, controlled_buffer_3_out[2], controlled_buffer_2_out[9]);
  Adder #(.width(1)) adder_211 (
    .a(and_212_out), .b(adder_197_out), .out(adder_211_out), .cin(adder_228_cout), .cout(adder_211_cout));
  and and_213 (and_213_out, controlled_buffer_3_out[1], controlled_buffer_2_out[13]);
  Adder #(.width(1)) adder_212 (
    .a(and_213_out), .b(adder_200_out), .out(adder_212_out), .cin(adder_229_cout), .cout(adder_212_cout));
  and and_214 (and_214_out, controlled_buffer_3_out[4], controlled_buffer_2_out[0]);
  Adder #(.width(1)) adder_213 (
    .a(and_214_out), .b(1'b0), .out(adder_213_out), .cin(adder_226_cout), .cout(adder_213_cout));
  Adder #(.width(1)) adder_214 (
    .a(and_211_out), .b(adder_201_out), .out(adder_214_out), .cin(adder_230_cout), .cout(adder_214_cout));
  and and_215 (and_215_out, controlled_buffer_3_out[2], controlled_buffer_2_out[8]);
  Adder #(.width(1)) adder_215 (
    .a(and_215_out), .b(adder_202_out), .out(adder_215_out), .cin(adder_231_cout), .cout(adder_215_cout));
  and and_216 (and_216_out, controlled_buffer_3_out[1], controlled_buffer_2_out[12]);
  Adder #(.width(1)) adder_216 (
    .a(and_216_out), .b(adder_203_out), .out(adder_216_out), .cin(adder_232_cout), .cout(adder_216_cout));
  and and_217 (and_217_out, controlled_buffer_3_out[3], controlled_buffer_2_out[3]);
  Adder #(.width(1)) adder_217 (
    .a(and_217_out), .b(adder_205_out), .out(adder_217_out), .cin(adder_233_cout), .cout(adder_217_cout));
  and and_218 (and_218_out, controlled_buffer_3_out[2], controlled_buffer_2_out[7]);
  Adder #(.width(1)) adder_218 (
    .a(and_218_out), .b(adder_206_out), .out(adder_218_out), .cin(adder_234_cout), .cout(adder_218_cout));
  and and_219 (and_219_out, controlled_buffer_3_out[1], controlled_buffer_2_out[11]);
  Adder #(.width(1)) adder_219 (
    .a(and_219_out), .b(adder_207_out), .out(adder_219_out), .cin(adder_235_cout), .cout(adder_219_cout));
  and and_220 (and_220_out, controlled_buffer_3_out[0], controlled_buffer_2_out[15]);
  and and_221 (and_221_out, controlled_buffer_3_out[3], controlled_buffer_2_out[2]);
  Adder #(.width(1)) adder_220 (
    .a(and_221_out), .b(adder_209_out), .out(adder_220_out), .cin(adder_236_cout), .cout(adder_220_cout));
  and and_222 (and_222_out, controlled_buffer_3_out[2], controlled_buffer_2_out[6]);
  and and_223 (and_223_out, controlled_buffer_3_out[1], controlled_buffer_2_out[10]);
  Adder #(.width(1)) adder_221 (
    .a(and_223_out), .b(adder_211_out), .out(adder_221_out), .cin(adder_238_cout), .cout(adder_221_cout));
  and and_224 (and_224_out, controlled_buffer_3_out[0], controlled_buffer_2_out[14]);
  Adder #(.width(1)) adder_222 (
    .a(and_220_out), .b(adder_208_out), .out(adder_256_out[15]), .cin(1'b0), .cout(adder_222_cout));
  and and_225 (and_225_out, controlled_buffer_3_out[3], controlled_buffer_2_out[1]);
  Adder #(.width(1)) adder_223 (
    .a(and_225_out), .b(adder_213_out), .out(adder_223_out), .cin(adder_239_cout), .cout(adder_223_cout));
  and and_226 (and_226_out, controlled_buffer_3_out[2], controlled_buffer_2_out[5]);
  Adder #(.width(1)) adder_224 (
    .a(and_222_out), .b(adder_210_out), .out(adder_224_out), .cin(adder_237_cout), .cout(adder_224_cout));
  and and_227 (and_227_out, controlled_buffer_3_out[1], controlled_buffer_2_out[9]);
  and and_228 (and_228_out, controlled_buffer_3_out[0], controlled_buffer_2_out[13]);
  Adder #(.width(1)) adder_225 (
    .a(and_224_out), .b(adder_212_out), .out(adder_256_out[14]), .cin(1'b0), .cout(adder_225_cout));
  and and_229 (and_229_out, controlled_buffer_3_out[3], controlled_buffer_2_out[0]);
  Adder #(.width(1)) adder_226 (
    .a(and_229_out), .b(1'b0), .out(adder_226_out), .cin(adder_242_cout), .cout(adder_226_cout));
  and and_230 (and_230_out, controlled_buffer_3_out[2], controlled_buffer_2_out[4]);
  Adder #(.width(1)) adder_227 (
    .a(and_226_out), .b(adder_214_out), .out(adder_227_out), .cin(adder_240_cout), .cout(adder_227_cout));
  and and_231 (and_231_out, controlled_buffer_3_out[1], controlled_buffer_2_out[8]);
  Adder #(.width(1)) adder_228 (
    .a(and_227_out), .b(adder_215_out), .out(adder_228_out), .cin(adder_241_cout), .cout(adder_228_cout));
  Adder #(.width(1)) adder_229 (
    .a(and_228_out), .b(adder_216_out), .out(adder_256_out[13]), .cin(1'b0), .cout(adder_229_cout));
  and and_232 (and_232_out, controlled_buffer_3_out[2], controlled_buffer_2_out[3]);
  Adder #(.width(1)) adder_230 (
    .a(and_230_out), .b(adder_217_out), .out(adder_230_out), .cin(adder_243_cout), .cout(adder_230_cout));
  and and_233 (and_233_out, controlled_buffer_3_out[1], controlled_buffer_2_out[7]);
  Adder #(.width(1)) adder_231 (
    .a(and_231_out), .b(adder_218_out), .out(adder_231_out), .cin(adder_245_cout), .cout(adder_231_cout));
  and and_234 (and_234_out, controlled_buffer_3_out[0], controlled_buffer_2_out[12]);
  Adder #(.width(1)) adder_232 (
    .a(and_234_out), .b(adder_219_out), .out(adder_256_out[12]), .cin(1'b0), .cout(adder_232_cout));
  Adder #(.width(1)) adder_233 (
    .a(and_232_out), .b(adder_220_out), .out(adder_233_out), .cin(adder_244_cout), .cout(adder_233_cout));
  and and_235 (and_235_out, controlled_buffer_3_out[1], controlled_buffer_2_out[6]);
  Adder #(.width(1)) adder_234 (
    .a(and_233_out), .b(adder_224_out), .out(adder_234_out), .cin(adder_247_cout), .cout(adder_234_cout));
  and and_236 (and_236_out, controlled_buffer_3_out[0], controlled_buffer_2_out[11]);
  Adder #(.width(1)) adder_235 (
    .a(and_236_out), .b(adder_221_out), .out(adder_256_out[11]), .cin(1'b0), .cout(adder_235_cout));
  and and_237 (and_237_out, controlled_buffer_3_out[2], controlled_buffer_2_out[2]);
  Adder #(.width(1)) adder_236 (
    .a(and_237_out), .b(adder_223_out), .out(adder_236_out), .cin(adder_246_cout), .cout(adder_236_cout));
  Adder #(.width(1)) adder_237 (
    .a(and_235_out), .b(adder_227_out), .out(adder_237_out), .cin(adder_248_cout), .cout(adder_237_cout));
  and and_238 (and_238_out, controlled_buffer_3_out[0], controlled_buffer_2_out[10]);
  Adder #(.width(1)) adder_238 (
    .a(and_238_out), .b(adder_228_out), .out(adder_256_out[10]), .cin(1'b0), .cout(adder_238_cout));
  and and_239 (and_239_out, controlled_buffer_3_out[2], controlled_buffer_2_out[1]);
  Adder #(.width(1)) adder_239 (
    .a(and_239_out), .b(adder_226_out), .out(adder_239_out), .cin(adder_249_cout), .cout(adder_239_cout));
  and and_240 (and_240_out, controlled_buffer_3_out[1], controlled_buffer_2_out[5]);
  Adder #(.width(1)) adder_240 (
    .a(and_240_out), .b(adder_230_out), .out(adder_240_out), .cin(adder_250_cout), .cout(adder_240_cout));
  and and_241 (and_241_out, controlled_buffer_3_out[0], controlled_buffer_2_out[9]);
  Adder #(.width(1)) adder_241 (
    .a(and_241_out), .b(adder_231_out), .out(adder_256_out[9]), .cin(1'b0), .cout(adder_241_cout));
  and and_242 (and_242_out, controlled_buffer_3_out[2], controlled_buffer_2_out[0]);
  Adder #(.width(1)) adder_242 (
    .a(and_242_out), .b(1'b0), .out(adder_242_out), .cin(adder_251_cout), .cout(adder_242_cout));
  and and_243 (and_243_out, controlled_buffer_3_out[1], controlled_buffer_2_out[4]);
  Adder #(.width(1)) adder_243 (
    .a(and_243_out), .b(adder_233_out), .out(adder_243_out), .cin(adder_252_cout), .cout(adder_243_cout));
  and and_244 (and_244_out, controlled_buffer_3_out[0], controlled_buffer_2_out[8]);
  and and_245 (and_245_out, controlled_buffer_3_out[1], controlled_buffer_2_out[3]);
  Adder #(.width(1)) adder_244 (
    .a(and_245_out), .b(adder_236_out), .out(adder_244_out), .cin(adder_253_cout), .cout(adder_244_cout));
  and and_246 (and_246_out, controlled_buffer_3_out[0], controlled_buffer_2_out[7]);
  Adder #(.width(1)) adder_245 (
    .a(and_244_out), .b(adder_234_out), .out(adder_256_out[8]), .cin(1'b0), .cout(adder_245_cout));
  and and_247 (and_247_out, controlled_buffer_3_out[1], controlled_buffer_2_out[2]);
  Adder #(.width(1)) adder_246 (
    .a(and_247_out), .b(adder_239_out), .out(adder_246_out), .cin(adder_254_cout), .cout(adder_246_cout));
  and and_248 (and_248_out, controlled_buffer_3_out[0], controlled_buffer_2_out[6]);
  Adder #(.width(1)) adder_247 (
    .a(and_246_out), .b(adder_237_out), .out(adder_256_out[7]), .cin(1'b0), .cout(adder_247_cout));
  and and_249 (and_249_out, controlled_buffer_3_out[1], controlled_buffer_2_out[1]);
  and and_250 (and_250_out, controlled_buffer_3_out[0], controlled_buffer_2_out[5]);
  Adder #(.width(1)) adder_248 (
    .a(and_248_out), .b(adder_240_out), .out(adder_256_out[6]), .cin(1'b0), .cout(adder_248_cout));
  and and_251 (and_251_out, controlled_buffer_3_out[1], controlled_buffer_2_out[0]);
  Adder #(.width(1)) adder_249 (
    .a(and_249_out), .b(adder_242_out), .out(adder_249_out), .cin(adder_255_cout), .cout(adder_249_cout));
  Adder #(.width(1)) adder_250 (
    .a(and_250_out), .b(adder_243_out), .out(adder_256_out[5]), .cin(1'b0), .cout(adder_250_cout));
  Adder #(.width(1)) adder_251 (
    .a(and_251_out), .b(1'b0), .out(adder_251_out), .cin(adder_256_cout), .cout(adder_251_cout));
  and and_252 (and_252_out, controlled_buffer_3_out[0], controlled_buffer_2_out[4]);
  Adder #(.width(1)) adder_252 (
    .a(and_252_out), .b(adder_244_out), .out(adder_256_out[4]), .cin(1'b0), .cout(adder_252_cout));
  and and_253 (and_253_out, controlled_buffer_3_out[0], controlled_buffer_2_out[3]);
  Adder #(.width(1)) adder_253 (
    .a(and_253_out), .b(adder_246_out), .out(adder_256_out[3]), .cin(1'b0), .cout(adder_253_cout));
  and and_254 (and_254_out, controlled_buffer_3_out[0], controlled_buffer_2_out[2]);
  Adder #(.width(1)) adder_254 (
    .a(and_254_out), .b(adder_249_out), .out(adder_256_out[2]), .cin(1'b0), .cout(adder_254_cout));
  and and_255 (and_255_out, controlled_buffer_3_out[0], controlled_buffer_2_out[1]);
  Adder #(.width(1)) adder_255 (
    .a(and_255_out), .b(adder_251_out), .out(adder_256_out[1]), .cin(1'b0), .cout(adder_255_cout));
  and and_256 (and_256_out, controlled_buffer_3_out[0], controlled_buffer_2_out[0]);
  Adder #(.width(1)) adder_256 (.a(and_256_out), .b(1'b0), .out(adder_256_out[0]), .cin(1'b0), .cout(adder_256_cout));
  assign controlled_buffer_1_out = FLAG_EDIT ? FLAG_IN : 8'bz;  // Controlled_Buffer controlled_buffer_1
  assign controlled_buffer_2_out = MUL_EN ? B_IN : 16'bz;  // Controlled_Buffer controlled_buffer_2
  assign controlled_buffer_3_out = MUL_EN ? A_IN : 16'bz;  // Controlled_Buffer controlled_buffer_3
  Priority_Encoder priority_encoder_1 (
    .in0(MUL), .in1(R_SFT), .in2(L_SFT), .in3(A_ND), .in4(O_R), .in5(X_OR), .in6(CMP), .in7(SUM),
    .out(priority_encoder_1_out));  // open: en_in, gs, en_out
  assign and_257_out = A_IN & B_IN;  // AND_Gate and_257, 16 bits wide
  assign or_1_out = A_IN | B_IN;  // OR_Gate or_1, 16 bits wide
  assign xor_2_out = A_IN ^ B_IN;  // XOR_Gate xor_2, 16 bits wide
  Subtractor #(.width(16)) subtractor_1 (.a(A_IN), .b(B_IN), .out(subtractor_1_out));  // open: bin, bout
  xor xor_3 (xor_3_out, B_IN[0], SUB);
  xor xor_4 (xor_4_out, B_IN[1], SUB);
  xor xor_5 (xor_5_out, B_IN[2], SUB);
  xor xor_6 (xor_6_out, B_IN[3], SUB);
  xor xor_7 (xor_7_out, B_IN[4], SUB);
  xor xor_8 (xor_8_out, B_IN[5], SUB);
  xor xor_9 (xor_9_out, B_IN[6], SUB);
  buf xor_10 (xor_10_out, SUB);  // XOR_Gate
  xor xor_11 (xor_11_out, B_IN[8], SUB);
  xor xor_12 (xor_12_out, B_IN[9], SUB);
  xor xor_13 (xor_13_out, B_IN[10], SUB);
  xor xor_14 (xor_14_out, B_IN[11], SUB);
  xor xor_15 (xor_15_out, B_IN[12], SUB);
  xor xor_16 (xor_16_out, B_IN[13], SUB);
  xor xor_17 (xor_17_out, B_IN[14], SUB);
  xor xor_18 (xor_18_out, B_IN[15], SUB);
  nor nor_1 (nor_1_out, subtractor_1_out[0], subtractor_1_out[1], subtractor_1_out[2], subtractor_1_out[3], subtractor_1_out[4], subtractor_1_out[5], subtractor_1_out[6], subtractor_1_out[7], subtractor_1_out[8], subtractor_1_out[9], subtractor_1_out[10], subtractor_1_out[11], subtractor_1_out[12], subtractor_1_out[13], subtractor_1_out[14], subtractor_1_out[15]);
  Multiplexer #(.enable("true"), .select(3), .width(16)) multiplexer_2 (
    .in0(adder_256_out), .in1({CARRY_F, A_IN[15:1]}), .in2({A_IN[14:0], CARRY_F}), .in3(and_257_out),
    .in4(or_1_out), .in5(xor_2_out), .in6(subtractor_1_out), .in7(adder_257_out), .out(ALU_OUT),
    .sel(priority_encoder_1_out), .en(ALU_EN));
  and and_258 (controlled_buffer_4_out[2], CMP, nor_1_out);
  Adder #(.width(1)) adder_257 (.a(A_IN[0]), .b(xor_3_out), .out(adder_257_out[0]), .cin(SUB), .cout(adder_257_cout));
  Adder #(.width(1)) adder_258 (
    .a(A_IN[1]), .b(xor_4_out), .out(adder_257_out[1]), .cin(adder_257_cout), .cout(adder_258_cout));
  Adder #(.width(1)) adder_259 (
    .a(A_IN[2]), .b(xor_5_out), .out(adder_257_out[2]), .cin(adder_258_cout), .cout(adder_259_cout));
  Adder #(.width(1)) adder_260 (
    .a(A_IN[3]), .b(xor_6_out), .out(adder_257_out[3]), .cin(adder_259_cout), .cout(adder_260_cout));
  Adder #(.width(1)) adder_261 (
    .a(A_IN[4]), .b(xor_7_out), .out(adder_257_out[4]), .cin(adder_260_cout), .cout(adder_261_cout));
  Adder #(.width(1)) adder_262 (
    .a(A_IN[5]), .b(xor_8_out), .out(adder_257_out[5]), .cin(adder_261_cout), .cout(adder_262_cout));
  Adder #(.width(1)) adder_263 (
    .a(A_IN[6]), .b(xor_9_out), .out(adder_257_out[6]), .cin(adder_262_cout), .cout(adder_263_cout));
  Adder #(.width(1)) adder_264 (
    .a(A_IN[7]), .b(xor_10_out), .out(adder_257_out[7]), .cin(adder_263_cout),
    .cout(controlled_buffer_4_out[5]));
  Adder #(.width(1)) adder_265 (
    .a(A_IN[8]), .b(xor_11_out), .out(adder_257_out[8]), .cin(controlled_buffer_4_out[5]),
    .cout(adder_265_cout));
  Adder #(.width(1)) adder_266 (
    .a(A_IN[9]), .b(xor_12_out), .out(adder_257_out[9]), .cin(adder_265_cout), .cout(adder_266_cout));
  Adder #(.width(1)) adder_267 (
    .a(A_IN[10]), .b(xor_13_out), .out(adder_257_out[10]), .cin(adder_266_cout), .cout(adder_267_cout));
  Adder #(.width(1)) adder_268 (
    .a(A_IN[11]), .b(xor_14_out), .out(adder_257_out[11]), .cin(adder_267_cout), .cout(adder_268_cout));
  Adder #(.width(1)) adder_269 (
    .a(A_IN[12]), .b(xor_15_out), .out(adder_257_out[12]), .cin(adder_268_cout), .cout(adder_269_cout));
  Adder #(.width(1)) adder_270 (
    .a(A_IN[13]), .b(xor_16_out), .out(adder_257_out[13]), .cin(adder_269_cout), .cout(adder_270_cout));
  Adder #(.width(1)) adder_271 (
    .a(A_IN[14]), .b(xor_17_out), .out(adder_257_out[14]), .cin(adder_270_cout),
    .cout(controlled_buffer_4_out[3]));
  Adder #(.width(1)) adder_272 (
    .a(A_IN[15]), .b(xor_18_out), .out(adder_257_out[15]), .cin(controlled_buffer_4_out[3]),
    .cout(adder_272_cout));
  Pull_Resistor #(.pull(1)) pull_resistor_1 (.node(pull_resistor_1_node[3]));
  BitSelector #(.width(16)) bitselector_1 (
    .in(ALU_OUT), .out(controlled_buffer_4_out[1]), .sel({4{pull_resistor_1_node[3]}}));
  Multiplexer multiplexer_3 (.in0(A_IN[0]), .in1(A_IN[15]), .out(multiplexer_3_out), .sel(L_SFT));
  nor nor_2 (controlled_buffer_4_out[4], ALU_OUT[0], ALU_OUT[1], ALU_OUT[2], ALU_OUT[3], ALU_OUT[4], ALU_OUT[5], ALU_OUT[6], ALU_OUT[7], ALU_OUT[8], ALU_OUT[9], ALU_OUT[10], ALU_OUT[11], ALU_OUT[12], ALU_OUT[13], ALU_OUT[14], ALU_OUT[15]);
  assign controlled_buffer_4_out[0] = SFT_W_CRY ? multiplexer_3_out : 1'bz;  // Controlled_Buffer controlled_buffer_4
  assign controlled_buffer_4_out[0] = SUM ? adder_272_cout : 1'bz;  // Controlled_Buffer controlled_buffer_5
  not not_1 (not_1_out, FLAG_EDIT);
  Register register_1 (
    .D(controlled_buffer_1_out), .en(FLAG_WR), .clk(CLK),
    .Q({INT_F, T_F, H_F, ZERO_F, V_F, CMP_F, NEG_F, CARRY_F}), .clr(RST_FLAG_REG));
  assign controlled_buffer_1_out = not_1_out ? {INT_EN_FLAG, T_FLAG, controlled_buffer_4_out} : 8'bz;  // Controlled_Buffer controlled_buffer_6
endmodule

module INST_DECODER (
  input  [7:0] FLAGS_IN,
  input  [31:0] DATA_IN,
  output PORT_A_IN_OUT,
  output PORT_B_IN_OUT,
  output HLT,
  output RST,
  output NOP,
  output PORT_IN,
  output PORT_OUT_DATA,
  output PORT_OUT_RD,
  output [7:0] CFG_REG,
  output [23:0] CALL_RET_BR_ADD,
  output RJMP,
  output CLC,
  output CLNC,
  output CLZ,
  output CNZ,
  output BRE,
  output BRNE,
  output BRC,
  output BRNC,
  output RET,
  output RTC,
  output RTNC,
  output RTZ,
  output RTNZ,
  output CFG,
  output ADD,
  output SUB,
  output MUL,
  output CMP,
  output O_R,
  output A_ND,
  output X_OR,
  output SR,
  output SL,
  output MOV,
  output LDS,
  output STS,
  output LDI,
  output CALL,
  output JMP,
  output [15:0] RD,
  output [15:0] RS,
  output SRC,
  output SLC,
  output MULS,
  output [7:0] RJMP_JMP_L_ADD,
  output [15:0] DATA_OUT,
  output [15:0] ADD_OUT
);

  wire decoder_3_out10, decoder_4_out1, decoder_4_out2, decoder_4_out3, decoder_4_out4, decoder_4_out5,
       decoder_4_out6, decoder_4_out7, decoder_4_out8, decoder_4_out10, decoder_4_out11, decoder_4_out12,
       decoder_4_out13, decoder_4_out14, decoder_5_out0, not_1_out, not_2_out, or_1_out, or_2_out, or_3_out,
       or_4_out, or_5_out, or_6_out;
  wire [3:0] undriven;

  Decoder #(.select(4)) decoder_1 (
    .out0(PORT_A_IN_OUT), .out1(PORT_B_IN_OUT), .out2(HLT), .out3(RST), .out4(RJMP), .sel(DATA_IN[19:16]),
    .en(or_2_out));  // open: out5, out6, out7, out8, out9, out10, out11, out12, out13, out14, out15
  Decoder #(.select(4)) decoder_2 (
    .out0(PORT_IN), .out1(PORT_OUT_DATA), .out2(PORT_OUT_RD), .sel(DATA_IN[23:20]), .en(decoder_4_out14));  // open: out3, out4, out5, out6, out7, out8, out9, out10, out11, out12, out13, out14, out15
  Decoder #(.select(4)) decoder_3 (
    .out0(CFG_REG[0]), .out1(CFG_REG[1]), .out2(CFG_REG[2]), .out3(CFG_REG[3]), .out4(CFG_REG[4]),
    .out5(CFG_REG[5]), .out6(CFG_REG[6]), .out7(CFG_REG[7]), .out10(decoder_3_out10),
    .out11(decoder_3_out10), .sel(DATA_IN[23:20]), .en(CFG));  // open: out8, out9, out12, out13, out14, out15
  Decoder #(.select(4)) decoder_4 (
    .out0(NOP), .out1(decoder_4_out1), .out2(decoder_4_out2), .out3(decoder_4_out3), .out4(decoder_4_out4),
    .out5(decoder_4_out5), .out6(decoder_4_out6), .out7(decoder_4_out7), .out8(decoder_4_out8), .out9(RET),
    .out10(decoder_4_out10), .out11(decoder_4_out11), .out12(decoder_4_out12), .out13(decoder_4_out13),
    .out14(decoder_4_out14), .out15(CFG), .sel(DATA_IN[27:24]), .en(decoder_5_out0));
  Decoder #(.select(4)) decoder_5 (
    .out0(decoder_5_out0), .out1(ADD), .out2(SUB), .out3(MUL), .out4(CMP), .out5(O_R), .out6(A_ND),
    .out7(X_OR), .out8(SR), .out9(SL), .out10(MOV), .out11(LDS), .out12(STS), .out13(LDI), .out14(CALL),
    .out15(JMP), .sel(DATA_IN[31:28]), .en(1'b1));
  Decoder #(.select(4)) decoder_6 (
    .out0(RD[0]), .out1(RD[1]), .out2(RD[2]), .out3(RD[3]), .out4(RD[4]), .out5(RD[5]), .out6(RD[6]),
    .out7(RD[7]), .out8(RD[8]), .out9(RD[9]), .out10(RD[10]), .out11(RD[11]), .out12(RD[12]), .out13(RD[13]),
    .out14(RD[14]), .out15(RD[15]), .sel(DATA_IN[27:24]), .en(or_6_out));
  Decoder #(.select(4)) decoder_7 (
    .out0(RS[0]), .out1(RS[1]), .out2(RS[2]), .out3(RS[3]), .out4(RS[4]), .out5(RS[5]), .out6(RS[6]),
    .out7(RS[7]), .out8(RS[8]), .out9(RS[9]), .out10(RS[10]), .out11(RS[11]), .out12(RS[12]), .out13(RS[13]),
    .out14(RS[14]), .out15(RS[15]), .sel(DATA_IN[23:20]), .en(or_5_out));
  Decoder #(.select(4)) decoder_8 (
    .out12(SRC), .out14(SLC), .out15(MULS), .sel(DATA_IN[19:16]), .en(or_4_out));  // open: out0, out1, out2, out3, out4, out5, out6, out7, out8, out9, out10, out11, out13
  or or_1 (or_1_out, CALL, decoder_4_out1, decoder_4_out2, decoder_4_out3, decoder_4_out4, decoder_4_out5, decoder_4_out6, decoder_4_out7, decoder_4_out8, RET, decoder_4_out10, decoder_4_out11, decoder_4_out12, decoder_4_out13);
  or or_2 (or_2_out, PORT_IN, PORT_OUT_DATA, PORT_OUT_RD);
  or or_3 (or_3_out, CALL, JMP);
  assign RJMP_JMP_L_ADD = or_3_out ? {DATA_IN[19:16], DATA_IN[23:20]} : 8'bz;  // Controlled_Buffer controlled_buffer_1
  not not_1 (not_1_out, FLAGS_IN[0]);
  not not_2 (not_2_out, FLAGS_IN[4]);
  or or_4 (or_4_out, MUL, SR, SL);
  or or_5 (or_5_out, ADD, SUB, MUL, CMP, STS, O_R, A_ND, X_OR, MOV);
  or or_6 (or_6_out, PORT_OUT_RD, ADD, SUB, MUL, CMP, O_R, A_ND, X_OR, SR, SL, MOV, LDS, LDI);
  and and_1 (CLC, FLAGS_IN[0], decoder_4_out1);
  and and_2 (CLNC, not_1_out, decoder_4_out2);
  and and_3 (CLZ, FLAGS_IN[4], decoder_4_out3);
  and and_4 (CNZ, not_2_out, decoder_4_out4);
  and and_5 (BRE, FLAGS_IN[4], decoder_4_out5);
  and and_6 (BRNE, not_2_out, decoder_4_out6);
  and and_7 (BRC, FLAGS_IN[0], decoder_4_out7);
  and and_8 (BRNC, not_1_out, decoder_4_out8);
  and and_9 (RTC, FLAGS_IN[0], decoder_4_out10);
  and and_10 (RTNC, not_1_out, decoder_4_out11);
  and and_11 (RTZ, FLAGS_IN[4], decoder_4_out12);
  and and_12 (RTNZ, not_2_out, decoder_4_out13);
  assign CALL_RET_BR_ADD = or_1_out ? {DATA_IN[23:20], undriven, DATA_IN[15:0]} : 24'bz;  // Controlled_Buffer controlled_buffer_2

  assign ADD_OUT = DATA_IN[15:0];
  assign DATA_OUT = DATA_IN[15:0];
endmodule
module test (
  input  in_1,
  input  in_2,
  input  in_3,
  input  in_4,
  input  in_5,
  input  in_6,
  input  [6:0] in_7,
  input  [7:0] in_8,
  input  in_9,
  input  in_10,
  input  in_11,
  output [3:0] out_12,
  output [7:0] out_13
);

  wire clock_1_out, clock_2_out, clock_3_out, undriven, undriven_2, undriven_3, undriven_4, undriven_5,
       undriven_6, undriven_7, undriven_8, undriven_9, undriven_10, undriven_11, undriven_12, undriven_13,
       undriven_14, undriven_15, undriven_16;
  wire [7:0] counter_1_q;

  Priority_Encoder #(.select(4)) priority_encoder_1 (
    .in0(undriven), .in1(undriven_2), .in2(undriven_3), .in3(undriven_4), .in4(undriven_5), .in5(undriven_6),
    .in6(undriven_7), .in7(undriven_8), .in8(undriven_9), .in9(undriven_10), .in10(undriven_11),
    .in11(undriven_12), .in12(undriven_13), .in13(undriven_14), .in14(undriven_15), .in15(undriven_16),
    .out(out_12));  // open: gs, en_out, en_in
  Clock clock_1 (.out(clock_1_out));
  Counter counter_1 (
    .clr(in_1), .load(in_2), .up(in_3), .count(in_5), .clk(clock_1_out), .Q(counter_1_q));  // open: D, carry
  Clock clock_2 (.out(clock_2_out));
  RAM ram_1 (.addr(counter_1_q), .we(in_4), .oe(in_6), .clk(clock_2_out), .din(in_8), .dout(out_13));
  Hex_Digit_Display hex_digit_display_1 (.value(out_13[3:0]));  // open: dp
  Hex_Digit_Display hex_digit_display_2 (.value(out_13[3:0]));  // open: dp
  Hex_Digit_Display hex_digit_display_3 (.value(out_13[7:4]));  // open: dp
  Hex_Digit_Display hex_digit_display_4 (.value(out_13[7:4]));  // open: dp
  Clock clock_3 (.out(clock_3_out));
  TTY tty_1 (.data(in_7), .clk(clock_3_out), .we(in_9), .clr(in_10));
endmodule
